// Logisim project Ьase14_4.0.circ as structural Verilog: 6 circuits, main circuit main
module main (
  input  [2:0] in_1,
  input  [2:0] in_2,
  input  [2:0] in_3,
  input  [2:0] in_4,
  input  [2:0] in_5,
  input  [2:0] in_6,
  input  [2:0] in_7,
  input  [2:0] in_8,
  input  in_9,
  input  in_10,
  input  in_11,
  input  in_12,
  input  in_13,
  input  in_14,
  input  in_15,
  input  in_16,
  output [2:0] out_17,
  output [2:0] out_18
);

  wire and_3_out, and_4_out, and_5_out, and_6_out, and_7_out, and_8_out, and_9_out, and_10_out, and_11_out,
       and_12_out, and_13_out, and_14_out, and_15_out, arbiter_1_p4, cdm_8_mark5_1_p4, cdm_8_mark5_1_p5,
       cdm_8_mark5_1_p7, cdm_8_mark5_1_p8, cdm_8_mark5_1_p9, cdm_8_mark5_1_p10, cdm_8_mark5_1_p11,
       cdm_8_mark5_1_p12, Clk, code, comparator_1_eq, comparator_2_eq, comparator_3_eq, comparator_4_eq,
       comparator_5_eq, comparator_6_eq, comparator_7_eq, comparator_8_eq, d_ff_2_q, d_ff_3_qn, d_ff_4_qn,
       d_ff_5_q, d_ff_6_q, data, dX, dY, EVENT_HIT_AI_hit_x, EVENT_HIT_AI_hit_x_1, EVENT_HIT_AI_hit_x_1_2,
       EVENT_HIT_AI_hit_x_2, EVENT_HIT_AI_hit_x_2_2, EVENT_HIT_PLAYER_hit_x, EVENT_HIT_PLAYER_hit_x_1,
       EVENT_HIT_PLAYER_hit_x_1_2, EVENT_HIT_PLAYER_hit_x_2, EVENT_HIT_PLAYER_hit_x_2_2, freeze, game_active,
       I_O_sel, IAck, IRQ, L, mem, not_1_out, not_2_out, or_4_out, or_5_out, or_6_out, or_7_out, or_8_out,
       or_9_out, or_11_out, or_13_out, or_14_out, or_16_out, or_17_out, or_18_out, or_19_out, or_20_out,
       or_21_out, or_22_out, or_24_out, R, RAM, rd_wr, Reset, shift_register_1_out, shift_register_1_q0,
       shift_register_1_q1, shift_register_1_q2, shift_register_1_q3, shift_register_1_q4,
       shift_register_1_q5, shift_register_1_q6, shift_register_1_q7;
  wire [1:0] Angle_Reg_q, or_3_out, or_12_out;
  wire [2:0] priority_encoder_1_out, vec;
  wire [3:0] adder_1_out, adder_2_out, I_O_addr, register_1_q, register_2_q;
  wire [4:0] ai_1_ai_x, ai_1_ai_x_1, ai_1_ai_x_1_2, ball_1_ball_x, ball_1_ball_y, player_1_player_x_1,
       player_1_player_x_1_2, player_x, slope_x, slope_y;
  wire [6:0] bit_extender_1_out, keyboard_1_data;
  wire [7:0] bit_extender_2_out, cdm_8_mark5_1_p16, cdm_8_mark5_1_p17, d_ff_1_q, I_O_data;
  wire [7:4] cdm_8_mark5_1_p15;
  wire [31:0] ai_1_ai_screen_pixel, ball_1_out_10, ball_1_out_11, ball_1_out_12, ball_1_out_13,
       ball_1_out_14, ball_1_out_15, ball_1_out_16, ball_1_out_17, ball_1_out_18, ball_1_out_19,
       ball_1_out_20, ball_1_out_21, ball_1_out_22, ball_1_out_23, ball_1_out_24, ball_1_out_25,
       ball_1_out_26, ball_1_out_27, ball_1_out_28, ball_1_out_29, ball_1_out_30, ball_1_out_31,
       ball_1_out_32, ball_1_out_33, ball_1_out_34, ball_1_out_35, ball_1_out_36, ball_1_out_37,
       ball_1_out_38, ball_1_out_39, ball_1_out_40, ball_1_out_41, or_1_out, or_2_out,
       player_1_player_screen_pixel;

  Clock clock_1 (.out(Clk));
  // Probe on cdm_8_mark5_1_p8
  // Probe on cdm_8_mark5_1_p7
  // Probe on cdm_8_mark5_1_p5
  // Probe on cdm_8_mark5_1_p4
  // Probe on cdm_8_mark5_1_p11
  // Probe on cdm_8_mark5_1_p10
  // Probe on cdm_8_mark5_1_p9
  // CdM_8_mark5 cdm_8_mark5_1: pin names not known; wires that end beside it: IRQ, vec, IAck, cdm_8_mark5_1_p4, cdm_8_mark5_1_p5, Clk, cdm_8_mark5_1_p7, cdm_8_mark5_1_p8, cdm_8_mark5_1_p9, cdm_8_mark5_1_p10, cdm_8_mark5_1_p11, cdm_8_mark5_1_p12, mem, rd_wr, {cdm_8_mark5_1_p15, I_O_addr}, cdm_8_mark5_1_p16, cdm_8_mark5_1_p17
  Decoder decoder_1 (.out0(code), .out1(data), .sel(cdm_8_mark5_1_p12), .en(mem));
  assign I_O_data = not_1_out ? cdm_8_mark5_1_p16 : 8'bz;  // Controlled_Buffer controlled_buffer_1
  not not_1 (not_1_out, rd_wr);
  assign cdm_8_mark5_1_p17 = rd_wr ? I_O_data : 8'bz;  // Controlled_Buffer controlled_buffer_2
  ai ai_1 (
    .Clk(Clk), .game_active(game_active), .ball_x(ball_1_ball_x), .ball_y(ball_1_ball_y), .ball_dx(dX),
    .ball_dy(dY), .player_x(player_x), .ai_screen_pixel(ai_1_ai_screen_pixel), .ai_x(ai_1_ai_x),
    .ai_x_1(ai_1_ai_x_1), .ai_x_1_2(ai_1_ai_x_1_2));
  ball ball_1 (
    .dX(dX), .dY(dY), .game_active(game_active), .clk(Clk), .ball_x(ball_1_ball_x), .out_18(ball_1_out_18),
    .out_19(ball_1_out_19), .out_20(ball_1_out_20), .out_21(ball_1_out_21), .out_22(ball_1_out_22),
    .out_23(ball_1_out_23), .out_24(ball_1_out_24), .out_25(ball_1_out_25), .ball_y(ball_1_ball_y),
    .slope_x(slope_x), .slope_y(slope_y), .out_26(ball_1_out_26), .out_27(ball_1_out_27),
    .out_28(ball_1_out_28), .out_29(ball_1_out_29), .out_30(ball_1_out_30), .out_31(ball_1_out_31),
    .out_32(ball_1_out_32), .out_33(ball_1_out_33), .out_34(ball_1_out_34), .out_35(ball_1_out_35),
    .out_36(ball_1_out_36), .out_37(ball_1_out_37), .out_38(ball_1_out_38), .out_39(ball_1_out_39),
    .out_40(ball_1_out_40), .out_41(ball_1_out_41), .out_10(ball_1_out_10), .out_11(ball_1_out_11),
    .out_12(ball_1_out_12), .out_13(ball_1_out_13), .out_14(ball_1_out_14), .out_15(ball_1_out_15),
    .out_16(ball_1_out_16), .out_17(ball_1_out_17), .freeze(freeze), .player_x(player_x));
  player player_1 (
    .btnLeft(L), .btnRight(R), .game_active(game_active), .Clk(Clk),
    .player_screen_pixel(player_1_player_screen_pixel), .player_x(player_x),
    .player_x_1(player_1_player_x_1), .player_x_1_2(player_1_player_x_1_2));
  assign or_1_out = ai_1_ai_screen_pixel | ball_1_out_10;  // OR_Gate or_1, 32 bits wide
  assign or_2_out = ball_1_out_41 | player_1_player_screen_pixel;  // OR_Gate or_2, 32 bits wide
  and and_1 (I_O_sel, cdm_8_mark5_1_p15[4], cdm_8_mark5_1_p15[5], cdm_8_mark5_1_p15[6], cdm_8_mark5_1_p15[7], data);
  collisionCheck EVENT_HIT_AI (
    .player_x(ai_1_ai_x), .player_x_1(ai_1_ai_x_1), .player_x_1_2(ai_1_ai_x_1_2), .ball_x(ball_1_ball_x),
    .ball_y(ball_1_ball_y), .coordinateToCheck(5'b00001), .hit_x(EVENT_HIT_AI_hit_x),
    .hit_x_1(EVENT_HIT_AI_hit_x_1), .hit_x_1_2(EVENT_HIT_AI_hit_x_1_2), .hit_x_2(EVENT_HIT_AI_hit_x_2),
    .hit_x_2_2(EVENT_HIT_AI_hit_x_2_2));
  DotMatrix #(.inputtype("row"), .matrixcols(32), .matrixrows(32)) dotmatrix_1 (
    .row0(or_1_out), .row1(ball_1_out_11), .row2(ball_1_out_12), .row3(ball_1_out_13), .row4(ball_1_out_14),
    .row5(ball_1_out_15), .row6(ball_1_out_16), .row7(ball_1_out_17), .row8(ball_1_out_18),
    .row9(ball_1_out_19), .row10(ball_1_out_20), .row11(ball_1_out_21), .row12(ball_1_out_22),
    .row13(ball_1_out_23), .row14(ball_1_out_24), .row15(ball_1_out_25), .row16(ball_1_out_26),
    .row17(ball_1_out_27), .row18(ball_1_out_28), .row19(ball_1_out_29), .row20(ball_1_out_30),
    .row21(ball_1_out_31), .row22(ball_1_out_32), .row23(ball_1_out_33), .row24(ball_1_out_34),
    .row25(ball_1_out_35), .row26(ball_1_out_36), .row27(ball_1_out_37), .row28(ball_1_out_38),
    .row29(ball_1_out_39), .row30(ball_1_out_40), .row31(or_2_out));
  collisionCheck EVENT_HIT_PLAYER (
    .player_x(player_x), .player_x_1(player_1_player_x_1), .player_x_1_2(player_1_player_x_1_2),
    .ball_x(ball_1_ball_x), .ball_y(ball_1_ball_y), .coordinateToCheck(5'b11110),
    .hit_x(EVENT_HIT_PLAYER_hit_x), .hit_x_1(EVENT_HIT_PLAYER_hit_x_1),
    .hit_x_1_2(EVENT_HIT_PLAYER_hit_x_1_2), .hit_x_2(EVENT_HIT_PLAYER_hit_x_2),
    .hit_x_2_2(EVENT_HIT_PLAYER_hit_x_2_2));
  Comparator #(.width(5), .mode("unsigned")) comparator_1 (
    .a(ball_1_ball_y), .b({5{1'b0}}), .eq(comparator_1_eq));  // open: gt, lt
  Comparator #(.width(5), .mode("unsigned")) comparator_2 (
    .a(ball_1_ball_y), .b({5{1'b1}}), .eq(comparator_2_eq));  // open: gt, lt
  and and_2 (RAM, ~I_O_sel, data);  // AND_Gate
  ROM rom_1 (.addr({cdm_8_mark5_1_p15, I_O_addr}), .data(I_O_data), .sel(code));
  RAM ram_1 (.addr({cdm_8_mark5_1_p15, I_O_addr}), .data(I_O_data), .sel(RAM), .clk(Clk), .ld(rd_wr));  // open: clr
  or or_3 (or_3_out[0], EVENT_HIT_AI_hit_x, EVENT_HIT_AI_hit_x_1, EVENT_HIT_AI_hit_x_1_2, EVENT_HIT_AI_hit_x_2, EVENT_HIT_AI_hit_x_2_2);
  or or_4 (or_4_out, comparator_1_eq, comparator_2_eq);
  Button button_1 (.out(L));
  Button button_2 (.out(R));
  or or_5 (or_5_out, L, R);
  or or_6 (or_6_out, or_4_out, Reset);
  Button button_3 (.out(Reset));
  Register #(.width(4)) register_1 (
    .D(adder_1_out), .en(game_active), .Q(register_1_q), .clk(comparator_1_eq), .clr(or_19_out));
  S_R_Flip_Flop s_r_ff_1 (.S(or_5_out), .clk(Clk), .R(or_6_out), .Q(game_active));  // open: Qn, preset, reset, en
  Register #(.width(4)) register_2 (
    .D(adder_2_out), .en(game_active), .Q(register_2_q), .clk(comparator_2_eq), .clr(or_19_out));
  Comparator #(.width(4), .mode("unsigned")) comparator_3 (
    .a(I_O_addr), .b(4'b0000), .eq(comparator_3_eq));  // open: gt, lt
  and and_3 (and_3_out, comparator_3_eq, I_O_sel);
  Comparator #(.width(4), .mode("unsigned")) comparator_4 (
    .a(I_O_addr), .b(4'b0001), .eq(comparator_4_eq));  // open: gt, lt
  and and_4 (and_4_out, comparator_4_eq, I_O_sel);
  LED led_1 ();  // open: in
  LED led_2 ();  // open: in
  Hex_Digit_Display hex_digit_display_1 (.value(register_1_q));  // open: dp
  Hex_Digit_Display hex_digit_display_2 (.value(register_2_q));  // open: dp
  Adder #(.width(4)) adder_1 (.a(register_1_q), .b(4'b0001), .out(adder_1_out));  // open: cin, cout
  Adder #(.width(4)) adder_2 (.a(register_2_q), .b(4'b0001), .out(adder_2_out));  // open: cin, cout
  and and_5 (and_5_out, ~rd_wr, and_3_out);  // AND_Gate
  LED led_3 (.in(and_3_out));
  LED led_4 (.in(and_4_out));
  D_Flip_Flop d_ff_1 (.clk(and_5_out), .D(I_O_data[0]), .Q(d_ff_1_q[0]));  // open: Qn, preset, en, reset
  and and_6 (and_6_out, rd_wr, and_3_out);
  and and_7 (and_7_out, ~rd_wr, and_4_out);  // AND_Gate
  or or_7 (or_7_out, EVENT_HIT_AI_hit_x, EVENT_HIT_PLAYER_hit_x);
  or or_8 (or_8_out, EVENT_HIT_AI_hit_x_1, EVENT_HIT_AI_hit_x_2, EVENT_HIT_PLAYER_hit_x_1, EVENT_HIT_PLAYER_hit_x_2);
  or or_9 (or_9_out, EVENT_HIT_AI_hit_x_1_2, EVENT_HIT_PLAYER_hit_x_1_2, EVENT_HIT_AI_hit_x_2_2, EVENT_HIT_PLAYER_hit_x_2_2);
  or or_10 (or_3_out[1], EVENT_HIT_PLAYER_hit_x, EVENT_HIT_PLAYER_hit_x_1, EVENT_HIT_PLAYER_hit_x_1_2, EVENT_HIT_PLAYER_hit_x_2, EVENT_HIT_PLAYER_hit_x_2_2);
  Comparator #(.width(4), .mode("unsigned")) comparator_5 (
    .a(register_1_q), .b(4'b0101), .eq(comparator_5_eq));  // open: gt, lt
  Comparator #(.width(4), .mode("unsigned")) comparator_6 (
    .a(register_2_q), .b(4'b0101), .eq(comparator_6_eq));  // open: gt, lt
  assign I_O_data = and_6_out ? {d_ff_1_q[7], {6{1'b0}}, d_ff_1_q[0]} : 8'bz;  // Controlled_Buffer controlled_buffer_3
  Bit_Extender #(.out_width(7)) bit_extender_1 (.in(I_O_data), .out(bit_extender_1_out));
  TTY #(.rows(4), .cols(19), .trigger("falling")) tty_1 (.data(bit_extender_1_out), .clk(and_7_out));  // open: we, clr
  Keyboard #(.trigger("falling")) keyboard_1 (
    .clk(Clk), .re(and_8_out), .avail(d_ff_1_q[7]), .data(keyboard_1_data));  // open: clr
  and and_8 (and_8_out, rd_wr, and_4_out);
  or or_11 (or_11_out, EVENT_HIT_AI_hit_x_1, EVENT_HIT_PLAYER_hit_x_1);
  or or_12 (or_12_out[0], or_11_out, or_13_out);
  or or_13 (or_13_out, EVENT_HIT_AI_hit_x_1_2, EVENT_HIT_PLAYER_hit_x_1_2);
  or or_14 (or_14_out, EVENT_HIT_AI_hit_x_2, EVENT_HIT_PLAYER_hit_x_2);
  or or_15 (or_12_out[1], or_14_out, or_16_out);
  or or_16 (or_16_out, EVENT_HIT_AI_hit_x_2_2, EVENT_HIT_PLAYER_hit_x_2_2);
  or or_17 (or_17_out, or_3_out[0], or_3_out[1]);
  or or_18 (or_18_out, EVENT_HIT_PLAYER_hit_x_1_2, EVENT_HIT_PLAYER_hit_x_1, EVENT_HIT_PLAYER_hit_x);
  or or_19 (or_19_out, comparator_5_eq, Reset, comparator_6_eq);
  or or_20 (or_20_out, or_8_out, or_9_out);
  D_Flip_Flop #(.trigger("falling")) d_ff_2 (
    .clk(or_17_out), .D(dY), .Q(d_ff_2_q), .en(game_active));  // open: Qn, preset, reset
  and and_9 (and_9_out, or_18_out, or_21_out);
  or or_21 (or_21_out, L, R);
  and and_10 (and_10_out, d_ff_1_q[0], d_ff_1_q[7]);
  Comparator #(.width(5), .mode("unsigned")) comparator_7 (
    .a(ball_1_ball_x), .b({5{1'b0}}), .eq(comparator_7_eq));  // open: gt, lt
  Comparator #(.width(5), .mode("unsigned")) comparator_8 (
    .a(ball_1_ball_x), .b({5{1'b1}}), .eq(comparator_8_eq));  // open: gt, lt
  Register #(.width(2)) Angle_Reg (.D(or_12_out), .en(or_17_out), .Q(Angle_Reg_q), .clk(Clk), .clr(not_2_out));
  not not_2 (not_2_out, game_active);
  Multiplexer #(.select(2), .enable("false")) multiplexer_1 (
    .in0(d_ff_2_q), .in1(1'b0), .in2(1'b1), .in3(1'b0), .out(dY), .sel(or_3_out));
  D_Flip_Flop #(.trigger("falling")) d_ff_3 (.clk(Clk), .D(and_9_out), .Qn(d_ff_3_qn));  // open: Q, preset, en, reset
  and and_11 (and_11_out, d_ff_3_qn, and_9_out);
  assign I_O_data = and_12_out ? bit_extender_2_out : 8'bz;  // Controlled_Buffer controlled_buffer_4
  assign bit_extender_2_out = {{1{1'b0}}, keyboard_1_data};  // Bit_Extender bit_extender_2
  and and_12 (and_12_out, rd_wr, and_4_out);
  or or_22 (or_22_out, comparator_7_eq, comparator_8_eq);
  Multiplexer #(.select(2), .width(5), .enable("false")) multiplexer_2 (
    .in0(5'b01000), .in1(5'b10000), .in2({5{1'b1}}), .out(slope_x), .sel(Angle_Reg_q));  // open: in3
  Shift_Register #(.trigger("falling")) shift_register_1 (
    .shift(1'b1), .in(and_11_out), .clk(Clk), .out(shift_register_1_out), .q0(shift_register_1_q0),
    .q1(shift_register_1_q1), .q2(shift_register_1_q2), .q3(shift_register_1_q3), .q4(shift_register_1_q4),
    .q5(shift_register_1_q5), .q6(shift_register_1_q6), .q7(shift_register_1_q7));  // open: load, clr, d0, d1, d2, d3, d4, d5, d6, d7
  assign vec = arbiter_1_p4 ? 3'b010 : 3'bz;  // Controlled_Buffer controlled_buffer_5
  // arbiter arbiter_1: pin names not known; wires that end beside it: IRQ, IAck, Clk, arbiter_1_p4, and_10_out, and_12_out, 1'b0, 1'b0
  Multiplexer #(.select(2), .width(5), .enable("false")) multiplexer_3 (
    .in0({5{1'b1}}), .in1(5'b10000), .in2(5'b01000), .out(slope_y), .sel(Angle_Reg_q));  // open: in3
  D_Flip_Flop #(.trigger("falling")) d_ff_4 (
    .clk(Clk), .D(shift_register_1_out), .Qn(d_ff_4_qn));  // open: Q, preset, en, reset
  or or_23 (freeze, shift_register_1_q7, shift_register_1_q6, shift_register_1_q5, shift_register_1_q4, shift_register_1_q3, shift_register_1_q2, shift_register_1_q1, shift_register_1_q0);
  and and_13 (and_13_out, L, d_ff_5_q);
  and and_14 (and_14_out, d_ff_5_q, R);
  D_Flip_Flop #(.trigger("falling")) d_ff_5 (.clk(Clk), .D(and_15_out), .Q(d_ff_5_q));  // open: Qn, preset, en, reset
  and and_15 (and_15_out, d_ff_4_qn, shift_register_1_out);
  or or_24 (or_24_out, and_13_out, or_7_out, or_20_out, or_22_out, and_14_out);
  Priority_Encoder priority_encoder_1 (
    .in0(1'b1), .in1(or_8_out), .in2(or_9_out), .in3(comparator_8_eq), .in4(comparator_7_eq),
    .in5(and_13_out), .in6(and_14_out), .out(priority_encoder_1_out));  // open: in7, en_in, gs, en_out
  D_Flip_Flop #(.trigger("falling")) d_ff_6 (.clk(or_24_out), .D(dX), .Q(d_ff_6_q));  // open: Qn, preset, en, reset
  Priority_Encoder priority_encoder_2 (
    .in0(in_9), .in1(in_10), .in2(in_11), .in3(in_12), .in4(in_13), .in5(in_14), .in6(in_15), .in7(in_16),
    .out(out_18));  // open: en_in, gs, en_out
  Multiplexer #(.select(3), .enable("false")) multiplexer_4 (
    .in0(d_ff_6_q), .in1(1'b0), .in2(1'b1), .in3(1'b1), .in4(1'b0), .in5(1'b0), .in6(1'b1), .out(dX),
    .sel(priority_encoder_1_out));  // open: in7
  Multiplexer #(.select(3), .width(3), .enable("false")) multiplexer_5 (
    .in0(in_1), .in1(in_2), .in2(in_3), .in3(in_4), .in4(in_5), .in5(in_6), .in6(in_7), .in7(in_8),
    .out(out_17), .sel(out_18));
  // XNOR_Gate xnor_1 is placed but not wired

  // Notes on the sheet:
  //   EVENT_HIT_TOP_WALL
  //   EVENT_HIT_BOTTOM_WALL
  //   instr_mem
  //   data_mem
  //   contents of rom_1 (hex, n*v repeats v):
  //   cd ef d0 29 d6 1e d0 f0 d1 1 a1 c1 d1 13 c1 d1 80 c1 d9 c5 d5 ee 14 ce d0 f1 b1 a1 cf d9 d1 f1 f2 8c
  //   a e0 28 a6 ee 20 d7 73 6d 69 6c 65 20 66 61 63 65 20 3a 33 d 189*0 17
  //   AI
  //   PLAYER
  //   0xf0  -> status register 
  //   0xf1  -> data register 
  //   read  => keyboard
  //   write => terminal
  //   right_hit_any
  //   ld 0xF1 → клавиатура
  //   st 0xF1 → терминал
  //   center_hit_any
  //   left_hit_any
  //   border_hit
  //   corner_hit
  //   EVENT_HIT_RIGHT_WALL
  //   EVENT_HIT_LEFT_WALL
  //   ldi r0, 0xf0
  //   ldi r1, 1
  //   st r0, r1
  //   status = 10000000b  если символ готов 
  //   status = 00000001b  если прерывания разрешены 
  //   status = 10000001b  если и символ готов, и прерывания разрешены
  //   Чтобы разрешить прерывания от клавиатуры, программа должна записать 1 в бит 0 регистра 0xf0
endmodule

module player (
  input  btnLeft,
  input  btnRight,
  input  game_active,
  input  Clk,
  output [31:0] player_screen_pixel,
  output [4:0] player_x,
  output [4:0] player_x_1,
  output [4:0] player_x_1_2
);

  wire and_1_out, and_2_out, comparator_1_eq, comparator_2_eq, not_1_out;
  wire [4:0] multiplexer_1_out, multiplexer_2_out, multiplexer_3_out;
  wire [31:0] decoder_1_out0, shifter_1_out, shifter_2_out;

  not not_1 (not_1_out, game_active);
  Register #(.width(5), .trigger("falling")) X (.D(multiplexer_1_out), .Q(player_x), .clk(Clk));  // open: en, clr
  Multiplexer #(.width(5), .enable("false")) multiplexer_1 (
    .in0(multiplexer_3_out), .in1(5'b01111), .out(multiplexer_1_out), .sel(not_1_out));
  Decoder #(.select(5), .enable("false")) decoder_1 (
    .out0(decoder_1_out0[0]), .out1(decoder_1_out0[1]), .out2(decoder_1_out0[2]), .out3(decoder_1_out0[3]),
    .out4(decoder_1_out0[4]), .out5(decoder_1_out0[5]), .out6(decoder_1_out0[6]), .out7(decoder_1_out0[7]),
    .out8(decoder_1_out0[8]), .out9(decoder_1_out0[9]), .out10(decoder_1_out0[10]),
    .out11(decoder_1_out0[11]), .out12(decoder_1_out0[12]), .out13(decoder_1_out0[13]),
    .out14(decoder_1_out0[14]), .out15(decoder_1_out0[15]), .out16(decoder_1_out0[16]),
    .out17(decoder_1_out0[17]), .out18(decoder_1_out0[18]), .out19(decoder_1_out0[19]),
    .out20(decoder_1_out0[20]), .out21(decoder_1_out0[21]), .out22(decoder_1_out0[22]),
    .out23(decoder_1_out0[23]), .out24(decoder_1_out0[24]), .out25(decoder_1_out0[25]),
    .out26(decoder_1_out0[26]), .out27(decoder_1_out0[27]), .out28(decoder_1_out0[28]),
    .out29(decoder_1_out0[29]), .out30(decoder_1_out0[30]), .out31(decoder_1_out0[31]), .sel(player_x));
  Shifter #(.width(32)) shifter_1 (.in(decoder_1_out0), .\dist (5'b00001), .out(shifter_1_out));
  Shifter #(.width(32), .shift("lr")) shifter_2 (.in(decoder_1_out0), .\dist (5'b00001), .out(shifter_2_out));
  Adder #(.width(5)) adder_1 (.a(player_x), .b(5'b00001), .out(player_x_1));  // open: cin, cout
  Subtractor #(.width(5)) subtractor_1 (.a(player_x), .b(5'b00001), .out(player_x_1_2));  // open: bin, bout
  Comparator #(.width(5), .mode("unsigned")) comparator_1 (
    .a(player_x), .b(5'b11110), .eq(comparator_1_eq));  // open: gt, lt
  Comparator #(.width(5), .mode("unsigned")) comparator_2 (
    .a(player_x), .b(5'b00001), .eq(comparator_2_eq));  // open: gt, lt
  assign player_screen_pixel = shifter_1_out | decoder_1_out0 | shifter_2_out;  // OR_Gate or_1, 32 bits wide
  Multiplexer #(.width(5), .enable("false")) multiplexer_2 (
    .in0(player_x), .in1(player_x_1), .out(multiplexer_2_out), .sel(and_1_out));
  and and_1 (and_1_out, btnLeft, ~comparator_1_eq);  // AND_Gate
  and and_2 (and_2_out, btnRight, ~comparator_2_eq);  // AND_Gate
  Multiplexer #(.width(5), .enable("false")) multiplexer_3 (
    .in0(multiplexer_2_out), .in1(player_x_1_2), .out(multiplexer_3_out), .sel(and_2_out));

  // Other names for the same wires on the sheet: Left = btnLeft; Right = btnRight
endmodule

module ai (
  input  Clk,
  input  game_active,
  input  [4:0] ball_x,
  input  [4:0] ball_y,
  input  ball_dx,
  input  ball_dy,
  input  [4:0] player_x,
  output [31:0] ai_screen_pixel,
  output [4:0] ai_x,
  output [4:0] ai_x_1,
  output [4:0] ai_x_1_2
);

  wire and_1_out, and_2_out, comparator_1_eq, comparator_2_eq, comparator_3_gt, comparator_4_gt,
       comparator_5_eq, comparator_6_lt, Left, not_1_out, Right;
  wire [4:0] adder_3_out, bit_extender_3_out, multiplexer_1_out, multiplexer_4_out, multiplexer_5_out,
       multiplexer_7_out, multiplexer_8_out, subtractor_5_out;
  wire [7:0] adder_1_out, bit_extender_1_out, bit_extender_2_out, multiplexer_2_out, multiplexer_3_out,
       multiplexer_6_out, subtractor_1_out, subtractor_3_out, subtractor_4_out;
  wire [31:0] decoder_1_out0, shifter_1_out, shifter_2_out;

  not not_1 (not_1_out, game_active);
  assign bit_extender_1_out = {{3{1'b0}}, ball_x};  // Bit_Extender bit_extender_1
  assign bit_extender_2_out = {{3{1'b0}}, ball_y};  // Bit_Extender bit_extender_2
  Multiplexer #(.width(5), .enable("false")) multiplexer_1 (
    .in0(multiplexer_5_out), .in1(5'b01111), .out(multiplexer_1_out), .sel(not_1_out));
  Adder adder_1 (.a(bit_extender_1_out), .b(bit_extender_2_out), .out(adder_1_out));  // open: cin, cout
  Subtractor subtractor_1 (.a(bit_extender_1_out), .b(bit_extender_2_out), .out(subtractor_1_out));  // open: bin, bout
  Decoder #(.select(5), .enable("false")) decoder_1 (
    .out0(decoder_1_out0[0]), .out1(decoder_1_out0[1]), .out2(decoder_1_out0[2]), .out3(decoder_1_out0[3]),
    .out4(decoder_1_out0[4]), .out5(decoder_1_out0[5]), .out6(decoder_1_out0[6]), .out7(decoder_1_out0[7]),
    .out8(decoder_1_out0[8]), .out9(decoder_1_out0[9]), .out10(decoder_1_out0[10]),
    .out11(decoder_1_out0[11]), .out12(decoder_1_out0[12]), .out13(decoder_1_out0[13]),
    .out14(decoder_1_out0[14]), .out15(decoder_1_out0[15]), .out16(decoder_1_out0[16]),
    .out17(decoder_1_out0[17]), .out18(decoder_1_out0[18]), .out19(decoder_1_out0[19]),
    .out20(decoder_1_out0[20]), .out21(decoder_1_out0[21]), .out22(decoder_1_out0[22]),
    .out23(decoder_1_out0[23]), .out24(decoder_1_out0[24]), .out25(decoder_1_out0[25]),
    .out26(decoder_1_out0[26]), .out27(decoder_1_out0[27]), .out28(decoder_1_out0[28]),
    .out29(decoder_1_out0[29]), .out30(decoder_1_out0[30]), .out31(decoder_1_out0[31]), .sel(ai_x));
  Register #(.width(5), .trigger("falling")) register_1 (.D(multiplexer_1_out), .Q(ai_x), .clk(Clk));  // open: en, clr
  Multiplexer #(.width(8), .enable("false")) multiplexer_2 (
    .in0(adder_1_out), .in1(subtractor_1_out), .out(multiplexer_2_out), .sel(ball_dx));
  Shifter #(.width(32)) shifter_1 (.in(decoder_1_out0), .\dist (5'b00001), .out(shifter_1_out));
  Shifter #(.width(32), .shift("lr")) shifter_2 (.in(decoder_1_out0), .\dist (5'b00001), .out(shifter_2_out));
  Adder #(.width(5)) adder_2 (.a(ai_x), .b(5'b00001), .out(ai_x_1));  // open: cin, cout
  Subtractor #(.width(5)) subtractor_2 (.a(ai_x), .b(5'b00001), .out(ai_x_1_2));  // open: bin, bout
  Comparator #(.width(5), .mode("unsigned")) comparator_1 (
    .a(ai_x), .b(5'b11110), .eq(comparator_1_eq));  // open: gt, lt
  Comparator #(.width(5), .mode("unsigned")) comparator_2 (
    .a(ai_x), .b(5'b00001), .eq(comparator_2_eq));  // open: gt, lt
  // OR_Gate or_1 has open pins: in0=comparator_3_gt, in1=Right, out=open
  Comparator #(.width(5), .mode("unsigned")) comparator_3 (
    .a(multiplexer_8_out), .b(ai_x), .gt(comparator_3_gt), .eq(comparator_3_gt), .lt(Right));
  Multiplexer #(.width(8), .enable("false")) multiplexer_3 (
    .in0(multiplexer_2_out), .in1(subtractor_3_out), .out(multiplexer_3_out), .sel(multiplexer_2_out[7]));
  Subtractor subtractor_3 (.a({8{1'b0}}), .b(multiplexer_2_out), .out(subtractor_3_out));  // open: bin, bout
  assign ai_screen_pixel = shifter_1_out | decoder_1_out0 | shifter_2_out;  // OR_Gate or_2, 32 bits wide
  Multiplexer #(.width(5), .enable("false")) multiplexer_4 (
    .in0(ai_x), .in1(ai_x_1), .out(multiplexer_4_out), .sel(and_1_out));
  and and_1 (and_1_out, Left, ~comparator_1_eq);  // AND_Gate
  and and_2 (and_2_out, Right, ~comparator_2_eq);  // AND_Gate
  Subtractor subtractor_4 (.a(8'h3e), .b(multiplexer_3_out), .out(subtractor_4_out));  // open: bin, bout
  Comparator #(.mode("unsigned")) comparator_4 (
    .a(multiplexer_3_out), .b(8'h1f), .gt(comparator_4_gt));  // open: eq, lt
  Multiplexer #(.width(5), .enable("false")) multiplexer_5 (
    .in0(multiplexer_4_out), .in1(ai_x_1_2), .out(multiplexer_5_out), .sel(and_2_out));
  Multiplexer #(.width(8), .enable("false")) multiplexer_6 (
    .in0(multiplexer_3_out), .in1(subtractor_4_out), .out(multiplexer_6_out), .sel(comparator_4_gt));
  Comparator #(.width(5), .mode("unsigned")) comparator_5 (
    .a(multiplexer_8_out), .b(ai_x_1), .gt(Left), .eq(comparator_5_eq));  // open: lt
  Bit_Extender #(.out_width(5)) bit_extender_3 (.in(multiplexer_6_out), .out(bit_extender_3_out));
  // OR_Gate or_3 has open pins: in0=Left, in1=comparator_5_eq, out=open
  Subtractor #(.width(5)) subtractor_5 (
    .a(bit_extender_3_out), .b(5'b00001), .out(subtractor_5_out));  // open: bin, bout
  Adder #(.width(5)) adder_3 (.a(bit_extender_3_out), .b(5'b00001), .out(adder_3_out));  // open: cin, cout
  Comparator #(.width(5), .mode("unsigned")) comparator_6 (
    .a(bit_extender_3_out), .b(player_x), .lt(comparator_6_lt));  // open: gt, eq
  Multiplexer #(.width(5), .enable("false")) multiplexer_7 (
    .in0(subtractor_5_out), .in1(adder_3_out), .out(multiplexer_7_out), .sel(comparator_6_lt));
  Multiplexer #(.width(5), .enable("false")) multiplexer_8 (
    .in0(5'b01111), .in1(multiplexer_7_out), .out(multiplexer_8_out), .sel(ball_dy));
endmodule

module ball (
  input  dX,
  input  dY,
  input  game_active,
  input  clk,
  input  [4:0] slope_x,
  input  [4:0] slope_y,
  input  freeze,
  input  [4:0] player_x,
  output [4:0] ball_x,
  output [31:0] out_10,
  output [31:0] out_11,
  output [31:0] out_12,
  output [31:0] out_13,
  output [31:0] out_14,
  output [31:0] out_15,
  output [31:0] out_16,
  output [31:0] out_17,
  output [31:0] out_18,
  output [31:0] out_19,
  output [31:0] out_20,
  output [31:0] out_21,
  output [31:0] out_22,
  output [31:0] out_23,
  output [31:0] out_24,
  output [31:0] out_25,
  output [31:0] out_26,
  output [31:0] out_27,
  output [31:0] out_28,
  output [31:0] out_29,
  output [31:0] out_30,
  output [31:0] out_31,
  output [31:0] out_32,
  output [31:0] out_33,
  output [31:0] out_34,
  output [31:0] out_35,
  output [31:0] out_36,
  output [31:0] out_37,
  output [31:0] out_38,
  output [31:0] out_39,
  output [31:0] out_40,
  output [31:0] out_41,
  output [4:0] ball_y
);

  wire adder_1_cout, adder_2_cout, and_1_out, decoder_2_out0, decoder_2_out1, decoder_2_out2, decoder_2_out3,
       decoder_2_out4, decoder_2_out5, decoder_2_out6, decoder_2_out7, decoder_2_out8, decoder_2_out9,
       decoder_2_out10, decoder_2_out11, decoder_2_out12, decoder_2_out13, decoder_2_out14, decoder_2_out15,
       decoder_2_out16, decoder_2_out17, decoder_2_out18, decoder_2_out19, decoder_2_out20, decoder_2_out21,
       decoder_2_out22, decoder_2_out23, decoder_2_out24, decoder_2_out25, decoder_2_out26, decoder_2_out27,
       decoder_2_out28, decoder_2_out29, decoder_2_out30, decoder_2_out31, not_1_out, not_2_out, or_1_out,
       or_2_out;
  wire [4:0] adder_1_out, adder_2_out, adder_3_out, adder_4_out, Error_Reg_X_q, Error_Reg_Y_q,
       multiplexer_1_out, multiplexer_2_out, multiplexer_3_out, multiplexer_4_out, multiplexer_5_out,
       subtractor_1_out, subtractor_2_out;
  wire [31:0] decoder_1_out0;

  not not_1 (not_1_out, game_active);
  not not_2 (not_2_out, game_active);
  Register #(.width(5)) Error_Reg_X (.D(adder_1_out), .Q(Error_Reg_X_q), .clk(clk), .clr(not_1_out));  // open: en
  Register #(.width(5)) Error_Reg_Y (.D(adder_2_out), .Q(Error_Reg_Y_q), .clk(clk), .clr(not_2_out));  // open: en
  Multiplexer #(.width(5), .enable("false")) multiplexer_1 (
    .in0(multiplexer_4_out), .in1(5'b01111), .out(multiplexer_1_out), .sel(not_1_out));
  or or_1 (or_1_out, not_1_out, adder_1_cout);
  Adder #(.width(5)) adder_1 (.a(Error_Reg_X_q), .b(slope_x), .out(adder_1_out), .cout(adder_1_cout));  // open: cin
  Multiplexer #(.width(5), .enable("false")) multiplexer_2 (
    .in0(multiplexer_5_out), .in1(5'b01111), .out(multiplexer_2_out), .sel(not_2_out));
  or or_2 (or_2_out, not_2_out, adder_2_cout);
  Adder #(.width(5)) adder_2 (.a(Error_Reg_Y_q), .b(slope_y), .out(adder_2_out), .cout(adder_2_cout));  // open: cin
  Multiplexer #(.width(5), .enable("false")) multiplexer_3 (
    .in0(multiplexer_1_out), .in1(player_x), .out(multiplexer_3_out), .sel(freeze));
  and and_1 (and_1_out, or_2_out, ~freeze);  // AND_Gate
  Register #(.width(5)) X (.D(multiplexer_3_out), .en(or_1_out), .Q(ball_x), .clk(clk));  // open: clr
  Register #(.width(5)) Y (.D(multiplexer_2_out), .en(and_1_out), .Q(ball_y), .clk(clk));  // open: clr
  Adder #(.width(5)) adder_3 (.a(ball_x), .b(5'b00001), .out(adder_3_out));  // open: cin, cout
  Subtractor #(.width(5)) subtractor_1 (.a(ball_x), .b(5'b00001), .out(subtractor_1_out));  // open: bin, bout
  Adder #(.width(5)) adder_4 (.a(ball_y), .b(5'b00001), .out(adder_4_out));  // open: cin, cout
  Subtractor #(.width(5)) subtractor_2 (.a(ball_y), .b(5'b00001), .out(subtractor_2_out));  // open: bin, bout
  Multiplexer #(.width(5), .enable("false")) multiplexer_4 (
    .in0(adder_3_out), .in1(subtractor_1_out), .out(multiplexer_4_out), .sel(dX));
  Multiplexer #(.width(5), .enable("false")) multiplexer_5 (
    .in0(adder_4_out), .in1(subtractor_2_out), .out(multiplexer_5_out), .sel(dY));
  Decoder #(.select(5), .enable("false")) decoder_1 (
    .out0(decoder_1_out0[0]), .out1(decoder_1_out0[1]), .out2(decoder_1_out0[2]), .out3(decoder_1_out0[3]),
    .out4(decoder_1_out0[4]), .out5(decoder_1_out0[5]), .out6(decoder_1_out0[6]), .out7(decoder_1_out0[7]),
    .out8(decoder_1_out0[8]), .out9(decoder_1_out0[9]), .out10(decoder_1_out0[10]),
    .out11(decoder_1_out0[11]), .out12(decoder_1_out0[12]), .out13(decoder_1_out0[13]),
    .out14(decoder_1_out0[14]), .out15(decoder_1_out0[15]), .out16(decoder_1_out0[16]),
    .out17(decoder_1_out0[17]), .out18(decoder_1_out0[18]), .out19(decoder_1_out0[19]),
    .out20(decoder_1_out0[20]), .out21(decoder_1_out0[21]), .out22(decoder_1_out0[22]),
    .out23(decoder_1_out0[23]), .out24(decoder_1_out0[24]), .out25(decoder_1_out0[25]),
    .out26(decoder_1_out0[26]), .out27(decoder_1_out0[27]), .out28(decoder_1_out0[28]),
    .out29(decoder_1_out0[29]), .out30(decoder_1_out0[30]), .out31(decoder_1_out0[31]), .sel(ball_x));
  Decoder #(.select(5), .enable("false")) decoder_2 (
    .out0(decoder_2_out0), .out1(decoder_2_out1), .out2(decoder_2_out2), .out3(decoder_2_out3),
    .out4(decoder_2_out4), .out5(decoder_2_out5), .out6(decoder_2_out6), .out7(decoder_2_out7),
    .out8(decoder_2_out8), .out9(decoder_2_out9), .out10(decoder_2_out10), .out11(decoder_2_out11),
    .out12(decoder_2_out12), .out13(decoder_2_out13), .out14(decoder_2_out14), .out15(decoder_2_out15),
    .out16(decoder_2_out16), .out17(decoder_2_out17), .out18(decoder_2_out18), .out19(decoder_2_out19),
    .out20(decoder_2_out20), .out21(decoder_2_out21), .out22(decoder_2_out22), .out23(decoder_2_out23),
    .out24(decoder_2_out24), .out25(decoder_2_out25), .out26(decoder_2_out26), .out27(decoder_2_out27),
    .out28(decoder_2_out28), .out29(decoder_2_out29), .out30(decoder_2_out30), .out31(decoder_2_out31),
    .sel(ball_y));
  assign out_10 = decoder_2_out0 ? decoder_1_out0 : 32'bz;  // Controlled_Buffer controlled_buffer_1
  assign out_11 = decoder_2_out1 ? decoder_1_out0 : 32'bz;  // Controlled_Buffer controlled_buffer_2
  assign out_12 = decoder_2_out2 ? decoder_1_out0 : 32'bz;  // Controlled_Buffer controlled_buffer_3
  assign out_13 = decoder_2_out3 ? decoder_1_out0 : 32'bz;  // Controlled_Buffer controlled_buffer_4
  assign out_14 = decoder_2_out4 ? decoder_1_out0 : 32'bz;  // Controlled_Buffer controlled_buffer_5
  assign out_15 = decoder_2_out5 ? decoder_1_out0 : 32'bz;  // Controlled_Buffer controlled_buffer_6
  assign out_16 = decoder_2_out6 ? decoder_1_out0 : 32'bz;  // Controlled_Buffer controlled_buffer_7
  assign out_17 = decoder_2_out7 ? decoder_1_out0 : 32'bz;  // Controlled_Buffer controlled_buffer_8
  assign out_18 = decoder_2_out8 ? decoder_1_out0 : 32'bz;  // Controlled_Buffer controlled_buffer_9
  assign out_19 = decoder_2_out9 ? decoder_1_out0 : 32'bz;  // Controlled_Buffer controlled_buffer_10
  assign out_20 = decoder_2_out10 ? decoder_1_out0 : 32'bz;  // Controlled_Buffer controlled_buffer_11
  assign out_21 = decoder_2_out11 ? decoder_1_out0 : 32'bz;  // Controlled_Buffer controlled_buffer_12
  assign out_22 = decoder_2_out12 ? decoder_1_out0 : 32'bz;  // Controlled_Buffer controlled_buffer_13
  assign out_23 = decoder_2_out13 ? decoder_1_out0 : 32'bz;  // Controlled_Buffer controlled_buffer_14
  assign out_24 = decoder_2_out14 ? decoder_1_out0 : 32'bz;  // Controlled_Buffer controlled_buffer_15
  assign out_25 = decoder_2_out15 ? decoder_1_out0 : 32'bz;  // Controlled_Buffer controlled_buffer_16
  assign out_26 = decoder_2_out16 ? decoder_1_out0 : 32'bz;  // Controlled_Buffer controlled_buffer_17
  assign out_27 = decoder_2_out17 ? decoder_1_out0 : 32'bz;  // Controlled_Buffer controlled_buffer_18
  assign out_28 = decoder_2_out18 ? decoder_1_out0 : 32'bz;  // Controlled_Buffer controlled_buffer_19
  assign out_29 = decoder_2_out19 ? decoder_1_out0 : 32'bz;  // Controlled_Buffer controlled_buffer_20
  assign out_30 = decoder_2_out20 ? decoder_1_out0 : 32'bz;  // Controlled_Buffer controlled_buffer_21
  assign out_31 = decoder_2_out21 ? decoder_1_out0 : 32'bz;  // Controlled_Buffer controlled_buffer_22
  assign out_32 = decoder_2_out22 ? decoder_1_out0 : 32'bz;  // Controlled_Buffer controlled_buffer_23
  assign out_33 = decoder_2_out23 ? decoder_1_out0 : 32'bz;  // Controlled_Buffer controlled_buffer_24
  assign out_34 = decoder_2_out24 ? decoder_1_out0 : 32'bz;  // Controlled_Buffer controlled_buffer_25
  assign out_35 = decoder_2_out25 ? decoder_1_out0 : 32'bz;  // Controlled_Buffer controlled_buffer_26
  assign out_36 = decoder_2_out26 ? decoder_1_out0 : 32'bz;  // Controlled_Buffer controlled_buffer_27
  assign out_37 = decoder_2_out27 ? decoder_1_out0 : 32'bz;  // Controlled_Buffer controlled_buffer_28
  assign out_38 = decoder_2_out28 ? decoder_1_out0 : 32'bz;  // Controlled_Buffer controlled_buffer_29
  assign out_39 = decoder_2_out29 ? decoder_1_out0 : 32'bz;  // Controlled_Buffer controlled_buffer_30
  assign out_40 = decoder_2_out30 ? decoder_1_out0 : 32'bz;  // Controlled_Buffer controlled_buffer_31
  assign out_41 = decoder_2_out31 ? decoder_1_out0 : 32'bz;  // Controlled_Buffer controlled_buffer_32
  Pull_Resistor pull_resistor_1 (.node(out_41));
  Pull_Resistor pull_resistor_2 (.node(out_37));
  Pull_Resistor pull_resistor_3 (.node(out_36));
  Pull_Resistor pull_resistor_4 (.node(out_40));
  Pull_Resistor pull_resistor_5 (.node(out_35));
  Pull_Resistor pull_resistor_6 (.node(out_39));
  Pull_Resistor pull_resistor_7 (.node(out_38));
  Pull_Resistor pull_resistor_8 (.node(out_34));
  Pull_Resistor pull_resistor_9 (.node(out_29));
  Pull_Resistor pull_resistor_10 (.node(out_30));
  Pull_Resistor pull_resistor_11 (.node(out_32));
  Pull_Resistor pull_resistor_12 (.node(out_28));
  Pull_Resistor pull_resistor_13 (.node(out_31));
  Pull_Resistor pull_resistor_14 (.node(out_27));
  Pull_Resistor pull_resistor_15 (.node(out_26));
  Pull_Resistor pull_resistor_16 (.node(out_33));
  Pull_Resistor pull_resistor_17 (.node(out_24));
  Pull_Resistor pull_resistor_18 (.node(out_25));
  Pull_Resistor pull_resistor_19 (.node(out_22));
  Pull_Resistor pull_resistor_20 (.node(out_20));
  Pull_Resistor pull_resistor_21 (.node(out_18));
  Pull_Resistor pull_resistor_22 (.node(out_21));
  Pull_Resistor pull_resistor_23 (.node(out_23));
  Pull_Resistor pull_resistor_24 (.node(out_19));
  Pull_Resistor pull_resistor_25 (.node(out_16));
  Pull_Resistor pull_resistor_26 (.node(out_17));
  Pull_Resistor pull_resistor_27 (.node(out_10));
  Pull_Resistor pull_resistor_28 (.node(out_12));
  Pull_Resistor pull_resistor_29 (.node(out_15));
  Pull_Resistor pull_resistor_30 (.node(out_11));
  Pull_Resistor pull_resistor_31 (.node(out_14));
  Pull_Resistor pull_resistor_32 (.node(out_13));

  // Other names for the same wires on the sheet: player_y[4:0] = player_x
endmodule

module collisionCheck (
  input  [4:0] player_x,
  input  [4:0] player_x_1,
  input  [4:0] player_x_1_2,
  input  [4:0] ball_x,
  input  [4:0] ball_y,
  input  [4:0] coordinateToCheck,
  output hit_x,
  output hit_x_1,
  output hit_x_1_2,
  output hit_x_2,
  output hit_x_2_2
);

  wire comparator_1_eq, comparator_2_eq, comparator_3_eq, comparator_4_eq, comparator_5_lt, comparator_6_eq,
       comparator_7_eq, comparator_8_gt;
  wire [4:0] adder_1_out, subtractor_1_out;

  Adder #(.width(5)) adder_1 (.a(player_x), .b(5'b00010), .out(adder_1_out));  // open: cin, cout
  Subtractor #(.width(5)) subtractor_1 (.a(player_x), .b(5'b00010), .out(subtractor_1_out));  // open: bin, bout
  Comparator #(.width(5), .mode("unsigned")) comparator_1 (
    .a(player_x), .b(ball_x), .eq(comparator_1_eq));  // open: gt, lt
  Comparator #(.width(5), .mode("unsigned")) comparator_2 (
    .a(player_x_1), .b(ball_x), .eq(comparator_2_eq));  // open: gt, lt
  Comparator #(.width(5), .mode("unsigned")) comparator_3 (
    .a(player_x_1_2), .b(ball_x), .eq(comparator_3_eq));  // open: gt, lt
  Comparator #(.width(5)) comparator_4 (.a(ball_y), .b(coordinateToCheck), .eq(comparator_4_eq));  // open: gt, lt
  Comparator #(.width(5), .mode("unsigned")) comparator_5 (
    .a(player_x), .b(5'b11110), .lt(comparator_5_lt));  // open: gt, eq
  Comparator #(.width(5), .mode("unsigned")) comparator_6 (
    .a(adder_1_out), .b(ball_x), .eq(comparator_6_eq));  // open: gt, lt
  Comparator #(.width(5), .mode("unsigned")) comparator_7 (
    .a(subtractor_1_out), .b(ball_x), .eq(comparator_7_eq));  // open: gt, lt
  Comparator #(.width(5), .mode("unsigned")) comparator_8 (
    .a(player_x), .b(5'b00001), .gt(comparator_8_gt));  // open: eq, lt
  and and_1 (hit_x, comparator_1_eq, comparator_4_eq);
  and and_2 (hit_x_1, comparator_2_eq, comparator_4_eq);
  and and_3 (hit_x_1_2, comparator_3_eq, comparator_4_eq);
  and and_4 (hit_x_2, comparator_5_lt, comparator_6_eq, comparator_4_eq);
  and and_5 (hit_x_2_2, comparator_7_eq, comparator_4_eq);
endmodule

module clock_frequency_divider (
  input  in_1,
  input  in_2,
  input  in_3,
  input  in_4
);

  wire clock_1_out, clock_2_out, clock_3_out, counter_1_carry, counter_2_carry, counter_3_carry, t_ff_1_q,
       t_ff_2_q, t_ff_3_q;

  Clock clock_1 (.out(clock_1_out));
  Clock clock_2 (.out(clock_2_out));
  Counter #(.width(3), .max('h4)) counter_1 (
    .carry(counter_1_carry), .clk(clock_1_out));  // open: load, D, count, Q, clr
  Counter #(.width(3), .max('h4)) counter_2 (
    .load(1'b1), .D(3'b100), .count(in_1), .carry(counter_2_carry), .clk(clock_2_out), .clr(in_2));  // open: Q
  Clock clock_3 (.out(clock_3_out));
  Counter #(.width(3), .max('h4), .ongoal("stay")) counter_3 (
    .D(3'b111), .count(in_3), .carry(counter_3_carry), .clk(clock_3_out), .clr(in_4));  // open: load, Q
  LED led_1 (.in(t_ff_1_q));
  T_Flip_Flop t_ff_1 (.clk(counter_1_carry), .T(counter_1_carry), .Q(t_ff_1_q));  // open: Qn, preset, reset, en
  LED led_2 (.in(t_ff_2_q));
  T_Flip_Flop t_ff_2 (.clk(counter_2_carry), .T(1'b1), .Q(t_ff_2_q), .reset(in_2), .en(in_1));  // open: Qn, preset
  T_Flip_Flop t_ff_3 (.clk(counter_3_carry), .T(1'b1), .Q(t_ff_3_q), .reset(in_4), .en(in_3));  // open: Qn, preset
  LED led_3 (.in(t_ff_3_q));
endmodule
