// Logisim project Ьase17_19.0.circ as structural Verilog: 19 circuits, main circuit MAIN
module MAIN (
);

  wire clear_kbd, clk, kbd_enable, kbd_is_ready, L, main_logic_1_cdm8_clk, main_logic_1_cdm8_clk_2,
       main_logic_1_clear_name_screen, main_logic_1_clear_records_screen, main_logic_1_f1_write,
       main_logic_1_name_screen_enable, R, Reset_out, Set_Name;
  wire [3:0] main_logic_1_ai_fails, main_logic_1_hundred, main_logic_1_one, main_logic_1_player_fails,
       main_logic_1_ten;
  wire [6:0] kbd_data, main_logic_1_kbd_data_2, main_logic_1_records_data;
  wire [31:0] main_logic_1_out_7, main_logic_1_out_8, main_logic_1_out_10, main_logic_1_out_11,
       main_logic_1_out_13, main_logic_1_out_14, main_logic_1_out_15, main_logic_1_out_16,
       main_logic_1_out_17, main_logic_1_out_18, main_logic_1_out_19, main_logic_1_out_21,
       main_logic_1_out_22, main_logic_1_out_23, main_logic_1_out_24, main_logic_1_out_25,
       main_logic_1_out_26, main_logic_1_out_27, main_logic_1_out_28, main_logic_1_out_29,
       main_logic_1_out_30, main_logic_1_out_31, main_logic_1_out_32, main_logic_1_out_33,
       main_logic_1_out_34, main_logic_1_out_35, main_logic_1_out_36, main_logic_1_out_37,
       main_logic_1_out_38, main_logic_1_out_39, main_logic_1_out_40, main_logic_1_out_41;

  MAIN_LOGIC main_logic_1 (
    .btn_left(L), .btn_right(R), .btn_reset(Reset_out), .out_7(main_logic_1_out_7),
    .out_8(main_logic_1_out_8), .out_10(main_logic_1_out_10), .out_11(main_logic_1_out_11),
    .out_13(main_logic_1_out_13), .out_14(main_logic_1_out_14), .out_15(main_logic_1_out_15),
    .out_16(main_logic_1_out_16), .out_17(main_logic_1_out_17), .out_18(main_logic_1_out_18),
    .out_19(main_logic_1_out_19), .out_21(main_logic_1_out_21), .out_22(main_logic_1_out_22),
    .out_23(main_logic_1_out_23), .out_24(main_logic_1_out_24), .out_25(main_logic_1_out_25),
    .out_26(main_logic_1_out_26), .out_27(main_logic_1_out_27), .out_28(main_logic_1_out_28),
    .out_29(main_logic_1_out_29), .out_30(main_logic_1_out_30), .out_31(main_logic_1_out_31),
    .out_32(main_logic_1_out_32), .out_33(main_logic_1_out_33), .out_34(main_logic_1_out_34),
    .out_35(main_logic_1_out_35), .out_36(main_logic_1_out_36), .out_37(main_logic_1_out_37),
    .out_38(main_logic_1_out_38), .out_39(main_logic_1_out_39), .out_40(main_logic_1_out_40),
    .out_41(main_logic_1_out_41), .player_fails(main_logic_1_player_fails), .ai_fails(main_logic_1_ai_fails),
    .one(main_logic_1_one), .hundred(main_logic_1_hundred), .ten(main_logic_1_ten), .cdm8_clk_3(clk),
    .cdm8_clk_2(main_logic_1_cdm8_clk_2), .cdm8_clk(main_logic_1_cdm8_clk),
    .clear_records_screen(main_logic_1_clear_records_screen), .btn_input_name(Set_Name),
    .kbd_is_ready(kbd_is_ready), .kbd_data(kbd_data), .kbd_data_2(main_logic_1_kbd_data_2),
    .records_data(main_logic_1_records_data), .f1_write(main_logic_1_f1_write),
    .clear_name_screen(main_logic_1_clear_name_screen), .clear_kbd(clear_kbd),
    .name_screen_enable(main_logic_1_name_screen_enable), .kbd_enable(kbd_enable));
  DotMatrix #(.inputtype("row"), .matrixcols(32), .matrixrows(1)) dotmatrix_1 (.row0(main_logic_1_out_7));
  DotMatrix #(.inputtype("row"), .matrixcols(32), .matrixrows(30)) dotmatrix_2 (
    .row0(main_logic_1_out_8), .row1(main_logic_1_out_10), .row2(main_logic_1_out_11),
    .row3(main_logic_1_out_13), .row4(main_logic_1_out_14), .row5(main_logic_1_out_15),
    .row6(main_logic_1_out_16), .row7(main_logic_1_out_17), .row8(main_logic_1_out_18),
    .row9(main_logic_1_out_19), .row10(main_logic_1_out_21), .row11(main_logic_1_out_22),
    .row12(main_logic_1_out_23), .row13(main_logic_1_out_24), .row14(main_logic_1_out_25),
    .row15(main_logic_1_out_26), .row16(main_logic_1_out_27), .row17(main_logic_1_out_28),
    .row18(main_logic_1_out_29), .row19(main_logic_1_out_30), .row20(main_logic_1_out_31),
    .row21(main_logic_1_out_32), .row22(main_logic_1_out_33), .row23(main_logic_1_out_34),
    .row24(main_logic_1_out_35), .row25(main_logic_1_out_36), .row26(main_logic_1_out_37),
    .row27(main_logic_1_out_38), .row28(main_logic_1_out_39), .row29(main_logic_1_out_40));
  Button Reset (.out(Reset_out));
  DotMatrix #(.inputtype("row"), .matrixcols(32), .matrixrows(1)) dotmatrix_3 (.row0(main_logic_1_out_41));
  LED led_1 ();  // open: in
  LED led_2 ();  // open: in
  Hex_Digit_Display hex_digit_display_1 (.value(main_logic_1_player_fails));  // open: dp
  Hex_Digit_Display hex_digit_display_2 (.value(main_logic_1_ai_fails));  // open: dp
  Button button_1 (.out(L));
  Hex_Digit_Display hex_digit_display_3 (.value(main_logic_1_hundred));  // open: dp
  Button button_2 (.out(R));
  Hex_Digit_Display hex_digit_display_4 (.value(main_logic_1_ten));  // open: dp
  Hex_Digit_Display hex_digit_display_5 (.value(main_logic_1_one));  // open: dp
  TTY #(.rows(7), .cols(22), .trigger("falling")) tty_1 (
    .data(main_logic_1_records_data), .clk(main_logic_1_cdm8_clk_2), .we(main_logic_1_f1_write),
    .clr(main_logic_1_clear_records_screen));
  TTY #(.rows(1), .cols(22)) tty_2 (
    .data(main_logic_1_kbd_data_2), .clk(main_logic_1_cdm8_clk), .we(main_logic_1_name_screen_enable),
    .clr(main_logic_1_clear_name_screen));
  Keyboard keyboard_1 (.clk(clk), .re(kbd_enable), .clr(clear_kbd), .avail(kbd_is_ready), .data(kbd_data));
  Button button_3 (.out(Set_Name));

  // Notes on the sheet:
  //   PLAYER
  //   AI
  //   TV_TENNIS GAME
  //   PLAYER_SCORE
  //   UI
  //   RECORDS_TABLE
  //   CURRENT_NAME
  //   SET NAME TO START
endmodule

module clock_frequency_divider (
  input  [7:0] game_speed,
  output game_clk,
  output cdm8_clk
);

  wire counter_1_carry;

  Clock clock_1 (.out(cdm8_clk));
  Counter #(.ongoal("load")) counter_1 (
    .load(1'b1), .D(game_speed), .count(1'b1), .carry(counter_1_carry), .clk(cdm8_clk));  // open: Q, clr
  T_Flip_Flop t_ff_1 (.clk(counter_1_carry), .T(1'b1), .Q(game_clk), .en(1'b1));  // open: Qn, preset, reset
  LED led_1 (.in(game_clk));
endmodule

module MAIN_LOGIC (
  input  btn_left,
  input  btn_right,
  input  btn_reset,
  input  btn_input_name,
  input  kbd_is_ready,
  input  [6:0] kbd_data,
  output [31:0] out_7,
  output [31:0] out_8,
  output [3:0] player_fails,
  output [31:0] out_10,
  output [31:0] out_11,
  output [3:0] ai_fails,
  output [31:0] out_13,
  output [31:0] out_14,
  output [31:0] out_15,
  output [31:0] out_16,
  output [31:0] out_17,
  output [31:0] out_18,
  output [31:0] out_19,
  output clear_records_screen,
  output [31:0] out_21,
  output [31:0] out_22,
  output [31:0] out_23,
  output [31:0] out_24,
  output [31:0] out_25,
  output [31:0] out_26,
  output [31:0] out_27,
  output [31:0] out_28,
  output [31:0] out_29,
  output [31:0] out_30,
  output [31:0] out_31,
  output [31:0] out_32,
  output [31:0] out_33,
  output [31:0] out_34,
  output [31:0] out_35,
  output [31:0] out_36,
  output [31:0] out_37,
  output [31:0] out_38,
  output [31:0] out_39,
  output [31:0] out_40,
  output [31:0] out_41,
  output [3:0] hundred,
  output [3:0] ten,
  output [3:0] one,
  output cdm8_clk,
  output cdm8_clk_2,
  output cdm8_clk_3,
  output [6:0] records_data,
  output f1_write,
  output clear_name_screen,
  output clear_kbd,
  output name_screen_enable,
  output kbd_enable,
  output [6:0] kbd_data_2
);

  wire dX, dY, dy_1_hit_any, EVENT_HIT_AI_hit_x, EVENT_HIT_AI_hit_x_1, EVENT_HIT_AI_hit_x_1_2,
       EVENT_HIT_AI_hit_x_2, EVENT_HIT_AI_hit_x_2_2, EVENT_HIT_PLAYER_hit_x, EVENT_HIT_PLAYER_hit_x_1,
       EVENT_HIT_PLAYER_hit_x_1_2, EVENT_HIT_PLAYER_hit_x_2, EVENT_HIT_PLAYER_hit_x_2_2, freeze, game_active,
       game_clk, hit_ai, hit_player, interrupt_start, name_is_valid;
  wire [4:0] AI_ai_x, AI_ai_x_1, AI_ai_x_1_2, ball_x, ball_y, player_1_player_x_1, player_1_player_x_1_2,
       player_x, slope_x, slope_y;
  wire [7:0] divider_1_out, divider_1_rem, divider_2_out, divider_2_rem, game_speed, player_score;
  wire [31:0] AI_ai_screen_pixel, ball_1_out_10, ball_1_out_41, player_1_player_screen_pixel;

  clock_frequency_divider CLOCK (.game_speed(game_speed), .game_clk(game_clk), .cdm8_clk(cdm8_clk));
  ai AI (
    .game_clk(game_clk), .game_active(game_active), .ball_x(ball_x), .ball_y(ball_y), .ball_dx(dX),
    .ball_dy(dY), .player_x(player_x), .ai_screen_pixel(AI_ai_screen_pixel), .ai_x(AI_ai_x),
    .ai_x_1(AI_ai_x_1), .ai_x_1_2(AI_ai_x_1_2));
  ball ball_1 (
    .dX(dX), .dY(dY), .game_active(game_active), .game_clk(game_clk), .ball_x(ball_x), .out_18(out_17),
    .out_19(out_18), .out_20(out_19), .out_21(out_21), .out_22(out_22), .out_23(out_23), .out_24(out_24),
    .out_25(out_25), .ball_y(ball_y), .slope_x(slope_x), .slope_y(slope_y), .out_26(out_26), .out_27(out_27),
    .out_28(out_28), .out_29(out_29), .out_30(out_30), .out_31(out_31), .out_32(out_32), .out_33(out_33),
    .out_34(out_34), .out_35(out_35), .out_36(out_36), .out_37(out_37), .out_38(out_38), .out_39(out_39),
    .out_40(out_40), .out_41(ball_1_out_41), .out_10(ball_1_out_10), .out_11(out_8), .out_12(out_10),
    .out_13(out_11), .out_14(out_13), .out_15(out_14), .out_16(out_15), .out_17(out_16), .freeze(freeze),
    .player_x(player_x));
  player player_1 (
    .btn_left(btn_left), .btn_right(btn_right), .game_active(game_active), .game_clk(game_clk),
    .player_screen_pixel(player_1_player_screen_pixel), .player_x(player_x),
    .player_x_1(player_1_player_x_1), .player_x_1_2(player_1_player_x_1_2));
  PROCESSOR_LOGIC processor_logic_1 (
    .cdm8_clk(cdm8_clk), .player_loser(clear_records_screen), .player_score(player_score),
    .I_O_data_read(records_data), .f1_write(f1_write), .interrupt_start(interrupt_start),
    .name_is_valid(name_is_valid), .btn_reset(btn_reset), .game_active(game_active),
    .btn_input_name(btn_input_name), .kbd_is_ready(kbd_is_ready), .kbd_data(kbd_data),
    .clear_name_screen(clear_name_screen), .clear_kbd(clear_kbd), .name_screen_enable(name_screen_enable),
    .kbd_enable(kbd_enable));
  collision_check EVENT_HIT_AI (
    .player_x(AI_ai_x), .player_x_1(AI_ai_x_1), .player_x_1_2(AI_ai_x_1_2), .ball_x(ball_x), .ball_y(ball_y),
    .coordinate_to_check(5'b00001), .hit_x(EVENT_HIT_AI_hit_x), .hit_x_1(EVENT_HIT_AI_hit_x_1),
    .hit_x_1_2(EVENT_HIT_AI_hit_x_1_2), .hit_x_2(EVENT_HIT_AI_hit_x_2), .hit_x_2_2(EVENT_HIT_AI_hit_x_2_2));
  assign out_7 = AI_ai_screen_pixel | ball_1_out_10;  // OR_Gate or_1, 32 bits wide
  assign out_41 = ball_1_out_41 | player_1_player_screen_pixel;  // OR_Gate or_2, 32 bits wide
  collision_check EVENT_HIT_PLAYER (
    .player_x(player_x), .player_x_1(player_1_player_x_1), .player_x_1_2(player_1_player_x_1_2),
    .ball_x(ball_x), .ball_y(ball_y), .coordinate_to_check(5'b11110), .hit_x(EVENT_HIT_PLAYER_hit_x),
    .hit_x_1(EVENT_HIT_PLAYER_hit_x_1), .hit_x_1_2(EVENT_HIT_PLAYER_hit_x_1_2),
    .hit_x_2(EVENT_HIT_PLAYER_hit_x_2), .hit_x_2_2(EVENT_HIT_PLAYER_hit_x_2_2));
  or or_3 (hit_ai, EVENT_HIT_AI_hit_x, EVENT_HIT_AI_hit_x_1, EVENT_HIT_AI_hit_x_1_2, EVENT_HIT_AI_hit_x_2, EVENT_HIT_AI_hit_x_2_2);
  or or_4 (hit_player, EVENT_HIT_PLAYER_hit_x, EVENT_HIT_PLAYER_hit_x_1, EVENT_HIT_PLAYER_hit_x_1_2, EVENT_HIT_PLAYER_hit_x_2, EVENT_HIT_PLAYER_hit_x_2_2);
  freeze u_FREEZE (
    .game_clk(game_clk), .hit_x(EVENT_HIT_PLAYER_hit_x), .hit_x_1(EVENT_HIT_PLAYER_hit_x_1),
    .hit_x_1_2(EVENT_HIT_PLAYER_hit_x_1_2), .btn_left(btn_left), .btn_right(btn_right), .freeze(freeze));
  dX dx_1 (
    .game_clk(game_clk), .hit_ai_x(EVENT_HIT_AI_hit_x), .hit_ai_x_1(EVENT_HIT_AI_hit_x_1),
    .hit_ai_x_1_2(EVENT_HIT_AI_hit_x_1_2), .hit_ai_x_2(EVENT_HIT_AI_hit_x_2),
    .hit_ai_x_2_2(EVENT_HIT_AI_hit_x_2_2), .hit_player_x(EVENT_HIT_PLAYER_hit_x),
    .hit_player_x_1(EVENT_HIT_PLAYER_hit_x_1), .hit_player_x_1_2(EVENT_HIT_PLAYER_hit_x_1_2),
    .hit_player_x_2(EVENT_HIT_PLAYER_hit_x_2), .hit_player_x_2_2(EVENT_HIT_PLAYER_hit_x_2_2),
    .btn_left(btn_left), .btn_right(btn_right), .freeze(freeze), .ball_x(ball_x), .dX(dX));
  dY dy_1 (.hit_ai(hit_ai), .hit_player(hit_player), .game_active(game_active), .hit_any(dy_1_hit_any), .dY(dY));
  game_active game_active_1 (
    .ball_y(ball_y), .btn_left(btn_left), .btn_right(btn_right), .btn_reset(btn_reset), .game_clk(game_clk),
    .name_is_valid(name_is_valid), .player_fails(player_fails), .ai_fails(ai_fails),
    .player_loser(clear_records_screen), .game_active(game_active), .interrupt_start(interrupt_start));
  player_score_game_speed player_score_game_speed_1 (
    .hit_player(hit_player), .f1_wrtie(f1_write), .game_clk(game_clk), .game_speed(game_speed),
    .player_score(player_score), .btn_reset(btn_reset));
  Divider divider_1 (.a(player_score), .b(8'h64), .out(divider_1_out), .rem(divider_1_rem));  // open: upper
  Bit_Extender #(.out_width(4)) bit_extender_1 (.in(divider_1_out), .out(hundred));
  Bit_Extender #(.out_width(4)) bit_extender_2 (.in(divider_2_out), .out(ten));
  Divider divider_2 (.a(divider_1_rem), .b(8'ha), .out(divider_2_out), .rem(divider_2_rem));  // open: upper
  Bresenham BRESENHAM (
    .hit_ai_x_1(EVENT_HIT_AI_hit_x_1), .hit_ai_x_1_2(EVENT_HIT_AI_hit_x_1_2),
    .hit_ai_x_2(EVENT_HIT_AI_hit_x_2), .hit_ai_x_2_2(EVENT_HIT_AI_hit_x_2_2),
    .hit_player_x_1(EVENT_HIT_PLAYER_hit_x_1), .hit_player_x_1_2(EVENT_HIT_PLAYER_hit_x_1_2),
    .hit_player_x_2(EVENT_HIT_PLAYER_hit_x_2), .hit_player_x_2_2(EVENT_HIT_PLAYER_hit_x_2_2),
    .hit_any(dy_1_hit_any), .game_clk(game_clk), .game_active(game_active), .slope_x(slope_x),
    .slope_y(slope_y));
  Bit_Extender #(.out_width(4)) bit_extender_3 (.in(divider_2_rem), .out(one));

  assign cdm8_clk_2 = cdm8_clk;
  assign cdm8_clk_3 = cdm8_clk;
  assign kbd_data_2 = kbd_data;

  // Other names for the same wires on the sheet: L = btn_left; player_loser = clear_records_screen; R = btn_right;
  //   Reset = btn_reset

  // Notes on the sheet:
  //   GAME_LOGIC
  //   PLAYER
  //   PROCESSOR_LOGIC
  //   MATRIX
  //   hit_any
  //   GAME_ACTIVE
  //   PLAYER_SCORE | GAME_SPEED
  //   PLAYER_SCORE_TO_SCREEN
endmodule

module player (
  input  btn_left,
  input  btn_right,
  input  game_clk,
  input  game_active,
  output [31:0] player_screen_pixel,
  output [4:0] player_x,
  output [4:0] player_x_1,
  output [4:0] player_x_1_2
);

  wire and_1_out, and_2_out, comparator_1_eq, comparator_2_eq, not_1_out;
  wire [4:0] multiplexer_1_out, multiplexer_2_out, multiplexer_3_out;
  wire [31:0] decoder_1_out0, shifter_1_out, shifter_2_out;

  Multiplexer #(.width(5), .enable("false")) multiplexer_1 (
    .in0(multiplexer_3_out), .in1(5'b10000), .out(multiplexer_1_out), .sel(not_1_out));
  not not_1 (not_1_out, game_active);
  Register #(.width(5), .trigger("falling")) X (.D(multiplexer_1_out), .Q(player_x), .clk(game_clk));  // open: en, clr
  Decoder #(.select(5), .enable("false")) decoder_1 (
    .out0(decoder_1_out0[0]), .out1(decoder_1_out0[1]), .out2(decoder_1_out0[2]), .out3(decoder_1_out0[3]),
    .out4(decoder_1_out0[4]), .out5(decoder_1_out0[5]), .out6(decoder_1_out0[6]), .out7(decoder_1_out0[7]),
    .out8(decoder_1_out0[8]), .out9(decoder_1_out0[9]), .out10(decoder_1_out0[10]),
    .out11(decoder_1_out0[11]), .out12(decoder_1_out0[12]), .out13(decoder_1_out0[13]),
    .out14(decoder_1_out0[14]), .out15(decoder_1_out0[15]), .out16(decoder_1_out0[16]),
    .out17(decoder_1_out0[17]), .out18(decoder_1_out0[18]), .out19(decoder_1_out0[19]),
    .out20(decoder_1_out0[20]), .out21(decoder_1_out0[21]), .out22(decoder_1_out0[22]),
    .out23(decoder_1_out0[23]), .out24(decoder_1_out0[24]), .out25(decoder_1_out0[25]),
    .out26(decoder_1_out0[26]), .out27(decoder_1_out0[27]), .out28(decoder_1_out0[28]),
    .out29(decoder_1_out0[29]), .out30(decoder_1_out0[30]), .out31(decoder_1_out0[31]), .sel(player_x));
  Shifter #(.width(32)) shifter_1 (.in(decoder_1_out0), .\dist (5'b00001), .out(shifter_1_out));
  Shifter #(.width(32), .shift("lr")) shifter_2 (.in(decoder_1_out0), .\dist (5'b00001), .out(shifter_2_out));
  Adder #(.width(5)) adder_1 (.a(player_x), .b(5'b00001), .out(player_x_1));  // open: cin, cout
  Subtractor #(.width(5)) subtractor_1 (.a(player_x), .b(5'b00001), .out(player_x_1_2));  // open: bin, bout
  Comparator #(.width(5), .mode("unsigned")) comparator_1 (
    .a(player_x), .b(5'b11110), .eq(comparator_1_eq));  // open: gt, lt
  Comparator #(.width(5), .mode("unsigned")) comparator_2 (
    .a(player_x), .b(5'b00001), .eq(comparator_2_eq));  // open: gt, lt
  assign player_screen_pixel = shifter_1_out | decoder_1_out0 | shifter_2_out;  // OR_Gate or_1, 32 bits wide
  Multiplexer #(.width(5), .enable("false")) multiplexer_2 (
    .in0(player_x), .in1(player_x_1), .out(multiplexer_2_out), .sel(and_1_out));
  and and_1 (and_1_out, btn_left, ~comparator_1_eq);  // AND_Gate
  and and_2 (and_2_out, btn_right, ~comparator_2_eq);  // AND_Gate
  Multiplexer #(.width(5), .enable("false")) multiplexer_3 (
    .in0(multiplexer_2_out), .in1(player_x_1_2), .out(multiplexer_3_out), .sel(and_2_out));
endmodule

module ai (
  input  [4:0] ball_x,
  input  [4:0] ball_y,
  input  ball_dx,
  input  ball_dy,
  input  [4:0] player_x,
  input  game_clk,
  input  game_active,
  output [31:0] ai_screen_pixel,
  output [4:0] ai_x,
  output [4:0] ai_x_1,
  output [4:0] ai_x_1_2
);

  wire and_1_out, and_2_out, btn_left, btn_right, comparator_1_eq, comparator_2_eq, comparator_4_gt,
       comparator_5_lt, not_1_out;
  wire [4:0] adder_3_out, bit_extender_3_out, multiplexer_2_out, multiplexer_5_out, multiplexer_6_out,
       multiplexer_7_out, multiplexer_8_out, subtractor_5_out;
  wire [7:0] adder_1_out, bit_extender_1_out, bit_extender_2_out, multiplexer_1_out, multiplexer_3_out,
       multiplexer_4_out, subtractor_1_out, subtractor_2_out, subtractor_4_out;
  wire [31:0] decoder_1_out0, shifter_1_out, shifter_2_out;

  assign bit_extender_1_out = {{3{1'b0}}, ball_x};  // Bit_Extender bit_extender_1
  assign bit_extender_2_out = {{3{1'b0}}, ball_y};  // Bit_Extender bit_extender_2
  Adder adder_1 (.a(bit_extender_1_out), .b(bit_extender_2_out), .out(adder_1_out));  // open: cin, cout
  Subtractor subtractor_1 (.a(bit_extender_1_out), .b(bit_extender_2_out), .out(subtractor_1_out));  // open: bin, bout
  not not_1 (not_1_out, game_active);
  Multiplexer #(.width(8), .enable("false")) multiplexer_1 (
    .in0(adder_1_out), .in1(subtractor_1_out), .out(multiplexer_1_out), .sel(ball_dx));
  Multiplexer #(.width(5), .enable("false")) multiplexer_2 (
    .in0(multiplexer_6_out), .in1(5'b10000), .out(multiplexer_2_out), .sel(not_1_out));
  Subtractor subtractor_2 (.a({8{1'b0}}), .b(multiplexer_1_out), .out(subtractor_2_out));  // open: bin, bout
  Decoder #(.select(5), .enable("false")) decoder_1 (
    .out0(decoder_1_out0[0]), .out1(decoder_1_out0[1]), .out2(decoder_1_out0[2]), .out3(decoder_1_out0[3]),
    .out4(decoder_1_out0[4]), .out5(decoder_1_out0[5]), .out6(decoder_1_out0[6]), .out7(decoder_1_out0[7]),
    .out8(decoder_1_out0[8]), .out9(decoder_1_out0[9]), .out10(decoder_1_out0[10]),
    .out11(decoder_1_out0[11]), .out12(decoder_1_out0[12]), .out13(decoder_1_out0[13]),
    .out14(decoder_1_out0[14]), .out15(decoder_1_out0[15]), .out16(decoder_1_out0[16]),
    .out17(decoder_1_out0[17]), .out18(decoder_1_out0[18]), .out19(decoder_1_out0[19]),
    .out20(decoder_1_out0[20]), .out21(decoder_1_out0[21]), .out22(decoder_1_out0[22]),
    .out23(decoder_1_out0[23]), .out24(decoder_1_out0[24]), .out25(decoder_1_out0[25]),
    .out26(decoder_1_out0[26]), .out27(decoder_1_out0[27]), .out28(decoder_1_out0[28]),
    .out29(decoder_1_out0[29]), .out30(decoder_1_out0[30]), .out31(decoder_1_out0[31]), .sel(ai_x));
  Register #(.width(5), .trigger("falling")) register_1 (
    .D(multiplexer_2_out), .Q(ai_x), .clk(game_clk));  // open: en, clr
  Multiplexer #(.width(8), .enable("false")) multiplexer_3 (
    .in0(multiplexer_1_out), .in1(subtractor_2_out), .out(multiplexer_3_out), .sel(multiplexer_1_out[7]));
  Shifter #(.width(32)) shifter_1 (.in(decoder_1_out0), .\dist (5'b00001), .out(shifter_1_out));
  Shifter #(.width(32), .shift("lr")) shifter_2 (.in(decoder_1_out0), .\dist (5'b00001), .out(shifter_2_out));
  Adder #(.width(5)) adder_2 (.a(ai_x), .b(5'b00001), .out(ai_x_1));  // open: cin, cout
  Subtractor #(.width(5)) subtractor_3 (.a(ai_x), .b(5'b00001), .out(ai_x_1_2));  // open: bin, bout
  Comparator #(.width(5), .mode("unsigned")) comparator_1 (
    .a(ai_x), .b(5'b11110), .eq(comparator_1_eq));  // open: gt, lt
  Comparator #(.width(5), .mode("unsigned")) comparator_2 (
    .a(ai_x), .b(5'b00001), .eq(comparator_2_eq));  // open: gt, lt
  Comparator #(.width(5), .mode("unsigned")) comparator_3 (
    .a(multiplexer_8_out), .b(ai_x), .lt(btn_right));  // open: gt, eq
  Multiplexer #(.width(8), .enable("false")) multiplexer_4 (
    .in0(multiplexer_3_out), .in1(subtractor_4_out), .out(multiplexer_4_out), .sel(comparator_4_gt));
  Subtractor subtractor_4 (.a(8'h3e), .b(multiplexer_3_out), .out(subtractor_4_out));  // open: bin, bout
  Comparator #(.mode("unsigned")) comparator_4 (
    .a(multiplexer_3_out), .b(8'h1f), .gt(comparator_4_gt));  // open: eq, lt
  assign ai_screen_pixel = shifter_1_out | decoder_1_out0 | shifter_2_out;  // OR_Gate or_1, 32 bits wide
  Multiplexer #(.width(5), .enable("false")) multiplexer_5 (
    .in0(ai_x), .in1(ai_x_1), .out(multiplexer_5_out), .sel(and_1_out));
  and and_1 (and_1_out, btn_left, ~comparator_1_eq);  // AND_Gate
  and and_2 (and_2_out, btn_right, ~comparator_2_eq);  // AND_Gate
  Bit_Extender #(.out_width(5)) bit_extender_3 (.in(multiplexer_4_out), .out(bit_extender_3_out));
  Multiplexer #(.width(5), .enable("false")) multiplexer_6 (
    .in0(multiplexer_5_out), .in1(ai_x_1_2), .out(multiplexer_6_out), .sel(and_2_out));
  Subtractor #(.width(5)) subtractor_5 (
    .a(bit_extender_3_out), .b(5'b00001), .out(subtractor_5_out));  // open: bin, bout
  Adder #(.width(5)) adder_3 (.a(bit_extender_3_out), .b(5'b00001), .out(adder_3_out));  // open: cin, cout
  Comparator #(.width(5), .mode("unsigned")) comparator_5 (
    .a(bit_extender_3_out), .b(player_x), .lt(comparator_5_lt));  // open: gt, eq
  Comparator #(.width(5), .mode("unsigned")) comparator_6 (
    .a(multiplexer_8_out), .b(ai_x_1), .gt(btn_left));  // open: eq, lt
  Multiplexer #(.width(5), .enable("false")) multiplexer_7 (
    .in0(subtractor_5_out), .in1(adder_3_out), .out(multiplexer_7_out), .sel(comparator_5_lt));
  Multiplexer #(.width(5), .enable("false")) multiplexer_8 (
    .in0(5'b01111), .in1(multiplexer_7_out), .out(multiplexer_8_out), .sel(ball_dy));

  // Notes on the sheet:
  //   Ricochet off the RIGHT wall
  //   Ricochet off the LEFT wall
  //   Pred_X
endmodule

module ball (
  input  dX,
  input  dY,
  input  [4:0] slope_x,
  input  [4:0] slope_y,
  input  freeze,
  input  [4:0] player_x,
  input  game_clk,
  input  game_active,
  output [4:0] ball_x,
  output [31:0] out_10,
  output [31:0] out_11,
  output [31:0] out_12,
  output [31:0] out_13,
  output [31:0] out_14,
  output [31:0] out_15,
  output [31:0] out_16,
  output [31:0] out_17,
  output [31:0] out_18,
  output [31:0] out_19,
  output [31:0] out_20,
  output [31:0] out_21,
  output [31:0] out_22,
  output [31:0] out_23,
  output [31:0] out_24,
  output [31:0] out_25,
  output [31:0] out_26,
  output [31:0] out_27,
  output [31:0] out_28,
  output [31:0] out_29,
  output [31:0] out_30,
  output [31:0] out_31,
  output [31:0] out_32,
  output [31:0] out_33,
  output [31:0] out_34,
  output [31:0] out_35,
  output [31:0] out_36,
  output [31:0] out_37,
  output [31:0] out_38,
  output [31:0] out_39,
  output [31:0] out_40,
  output [31:0] out_41,
  output [4:0] ball_y
);

  wire adder_1_cout, adder_2_cout, and_1_out, decoder_2_out0, decoder_2_out1, decoder_2_out2, decoder_2_out3,
       decoder_2_out4, decoder_2_out5, decoder_2_out6, decoder_2_out7, decoder_2_out8, decoder_2_out9,
       decoder_2_out10, decoder_2_out11, decoder_2_out12, decoder_2_out13, decoder_2_out14, decoder_2_out15,
       decoder_2_out16, decoder_2_out17, decoder_2_out18, decoder_2_out19, decoder_2_out20, decoder_2_out21,
       decoder_2_out22, decoder_2_out23, decoder_2_out24, decoder_2_out25, decoder_2_out26, decoder_2_out27,
       decoder_2_out28, decoder_2_out29, decoder_2_out30, decoder_2_out31, not_1_out, not_2_out, or_1_out,
       or_2_out;
  wire [4:0] adder_1_out, adder_2_out, adder_3_out, adder_4_out, Error_Reg_X_q, Error_Reg_Y_q,
       multiplexer_1_out, multiplexer_2_out, multiplexer_3_out, multiplexer_4_out, multiplexer_5_out,
       subtractor_1_out, subtractor_2_out;
  wire [31:0] decoder_1_out0;

  not not_1 (not_1_out, game_active);
  not not_2 (not_2_out, game_active);
  Register #(.width(5)) Error_Reg_X (.D(adder_1_out), .Q(Error_Reg_X_q), .clk(game_clk), .clr(not_1_out));  // open: en
  Register #(.width(5)) Error_Reg_Y (.D(adder_2_out), .Q(Error_Reg_Y_q), .clk(game_clk), .clr(not_2_out));  // open: en
  Adder #(.width(5)) adder_1 (.a(Error_Reg_X_q), .b(slope_x), .out(adder_1_out), .cout(adder_1_cout));  // open: cin
  Adder #(.width(5)) adder_2 (.a(Error_Reg_Y_q), .b(slope_y), .out(adder_2_out), .cout(adder_2_cout));  // open: cin
  Multiplexer #(.width(5), .enable("false")) multiplexer_1 (
    .in0(multiplexer_4_out), .in1(5'b10000), .out(multiplexer_1_out), .sel(not_1_out));
  or or_1 (or_1_out, not_1_out, adder_1_cout);
  Multiplexer #(.width(5), .enable("false")) multiplexer_2 (
    .in0(multiplexer_5_out), .in1(5'b10000), .out(multiplexer_2_out), .sel(not_2_out));
  or or_2 (or_2_out, not_2_out, adder_2_cout);
  Multiplexer #(.width(5), .enable("false")) multiplexer_3 (
    .in0(multiplexer_1_out), .in1(player_x), .out(multiplexer_3_out), .sel(freeze));
  and and_1 (and_1_out, or_2_out, ~freeze);  // AND_Gate
  Register #(.width(5)) X (.D(multiplexer_3_out), .en(or_1_out), .Q(ball_x), .clk(game_clk));  // open: clr
  Register #(.width(5)) Y (.D(multiplexer_2_out), .en(and_1_out), .Q(ball_y), .clk(game_clk));  // open: clr
  Adder #(.width(5)) adder_3 (.a(ball_x), .b(5'b00001), .out(adder_3_out));  // open: cin, cout
  Subtractor #(.width(5)) subtractor_1 (.a(ball_x), .b(5'b00001), .out(subtractor_1_out));  // open: bin, bout
  Adder #(.width(5)) adder_4 (.a(ball_y), .b(5'b00001), .out(adder_4_out));  // open: cin, cout
  Subtractor #(.width(5)) subtractor_2 (.a(ball_y), .b(5'b00001), .out(subtractor_2_out));  // open: bin, bout
  Multiplexer #(.width(5), .enable("false")) multiplexer_4 (
    .in0(adder_3_out), .in1(subtractor_1_out), .out(multiplexer_4_out), .sel(dX));
  Multiplexer #(.width(5), .enable("false")) multiplexer_5 (
    .in0(adder_4_out), .in1(subtractor_2_out), .out(multiplexer_5_out), .sel(dY));
  Decoder #(.select(5), .enable("false")) decoder_1 (
    .out0(decoder_1_out0[0]), .out1(decoder_1_out0[1]), .out2(decoder_1_out0[2]), .out3(decoder_1_out0[3]),
    .out4(decoder_1_out0[4]), .out5(decoder_1_out0[5]), .out6(decoder_1_out0[6]), .out7(decoder_1_out0[7]),
    .out8(decoder_1_out0[8]), .out9(decoder_1_out0[9]), .out10(decoder_1_out0[10]),
    .out11(decoder_1_out0[11]), .out12(decoder_1_out0[12]), .out13(decoder_1_out0[13]),
    .out14(decoder_1_out0[14]), .out15(decoder_1_out0[15]), .out16(decoder_1_out0[16]),
    .out17(decoder_1_out0[17]), .out18(decoder_1_out0[18]), .out19(decoder_1_out0[19]),
    .out20(decoder_1_out0[20]), .out21(decoder_1_out0[21]), .out22(decoder_1_out0[22]),
    .out23(decoder_1_out0[23]), .out24(decoder_1_out0[24]), .out25(decoder_1_out0[25]),
    .out26(decoder_1_out0[26]), .out27(decoder_1_out0[27]), .out28(decoder_1_out0[28]),
    .out29(decoder_1_out0[29]), .out30(decoder_1_out0[30]), .out31(decoder_1_out0[31]), .sel(ball_x));
  Decoder #(.select(5), .enable("false")) decoder_2 (
    .out0(decoder_2_out0), .out1(decoder_2_out1), .out2(decoder_2_out2), .out3(decoder_2_out3),
    .out4(decoder_2_out4), .out5(decoder_2_out5), .out6(decoder_2_out6), .out7(decoder_2_out7),
    .out8(decoder_2_out8), .out9(decoder_2_out9), .out10(decoder_2_out10), .out11(decoder_2_out11),
    .out12(decoder_2_out12), .out13(decoder_2_out13), .out14(decoder_2_out14), .out15(decoder_2_out15),
    .out16(decoder_2_out16), .out17(decoder_2_out17), .out18(decoder_2_out18), .out19(decoder_2_out19),
    .out20(decoder_2_out20), .out21(decoder_2_out21), .out22(decoder_2_out22), .out23(decoder_2_out23),
    .out24(decoder_2_out24), .out25(decoder_2_out25), .out26(decoder_2_out26), .out27(decoder_2_out27),
    .out28(decoder_2_out28), .out29(decoder_2_out29), .out30(decoder_2_out30), .out31(decoder_2_out31),
    .sel(ball_y));
  assign out_10 = decoder_2_out0 ? decoder_1_out0 : 32'bz;  // Controlled_Buffer controlled_buffer_1
  assign out_11 = decoder_2_out1 ? decoder_1_out0 : 32'bz;  // Controlled_Buffer controlled_buffer_2
  assign out_12 = decoder_2_out2 ? decoder_1_out0 : 32'bz;  // Controlled_Buffer controlled_buffer_3
  assign out_13 = decoder_2_out3 ? decoder_1_out0 : 32'bz;  // Controlled_Buffer controlled_buffer_4
  assign out_14 = decoder_2_out4 ? decoder_1_out0 : 32'bz;  // Controlled_Buffer controlled_buffer_5
  assign out_15 = decoder_2_out5 ? decoder_1_out0 : 32'bz;  // Controlled_Buffer controlled_buffer_6
  assign out_16 = decoder_2_out6 ? decoder_1_out0 : 32'bz;  // Controlled_Buffer controlled_buffer_7
  assign out_17 = decoder_2_out7 ? decoder_1_out0 : 32'bz;  // Controlled_Buffer controlled_buffer_8
  assign out_18 = decoder_2_out8 ? decoder_1_out0 : 32'bz;  // Controlled_Buffer controlled_buffer_9
  assign out_19 = decoder_2_out9 ? decoder_1_out0 : 32'bz;  // Controlled_Buffer controlled_buffer_10
  assign out_20 = decoder_2_out10 ? decoder_1_out0 : 32'bz;  // Controlled_Buffer controlled_buffer_11
  assign out_21 = decoder_2_out11 ? decoder_1_out0 : 32'bz;  // Controlled_Buffer controlled_buffer_12
  assign out_22 = decoder_2_out12 ? decoder_1_out0 : 32'bz;  // Controlled_Buffer controlled_buffer_13
  assign out_23 = decoder_2_out13 ? decoder_1_out0 : 32'bz;  // Controlled_Buffer controlled_buffer_14
  assign out_24 = decoder_2_out14 ? decoder_1_out0 : 32'bz;  // Controlled_Buffer controlled_buffer_15
  assign out_25 = decoder_2_out15 ? decoder_1_out0 : 32'bz;  // Controlled_Buffer controlled_buffer_16
  assign out_26 = decoder_2_out16 ? decoder_1_out0 : 32'bz;  // Controlled_Buffer controlled_buffer_17
  assign out_27 = decoder_2_out17 ? decoder_1_out0 : 32'bz;  // Controlled_Buffer controlled_buffer_18
  assign out_28 = decoder_2_out18 ? decoder_1_out0 : 32'bz;  // Controlled_Buffer controlled_buffer_19
  assign out_29 = decoder_2_out19 ? decoder_1_out0 : 32'bz;  // Controlled_Buffer controlled_buffer_20
  assign out_30 = decoder_2_out20 ? decoder_1_out0 : 32'bz;  // Controlled_Buffer controlled_buffer_21
  assign out_31 = decoder_2_out21 ? decoder_1_out0 : 32'bz;  // Controlled_Buffer controlled_buffer_22
  assign out_32 = decoder_2_out22 ? decoder_1_out0 : 32'bz;  // Controlled_Buffer controlled_buffer_23
  assign out_33 = decoder_2_out23 ? decoder_1_out0 : 32'bz;  // Controlled_Buffer controlled_buffer_24
  assign out_34 = decoder_2_out24 ? decoder_1_out0 : 32'bz;  // Controlled_Buffer controlled_buffer_25
  assign out_35 = decoder_2_out25 ? decoder_1_out0 : 32'bz;  // Controlled_Buffer controlled_buffer_26
  assign out_36 = decoder_2_out26 ? decoder_1_out0 : 32'bz;  // Controlled_Buffer controlled_buffer_27
  assign out_37 = decoder_2_out27 ? decoder_1_out0 : 32'bz;  // Controlled_Buffer controlled_buffer_28
  assign out_38 = decoder_2_out28 ? decoder_1_out0 : 32'bz;  // Controlled_Buffer controlled_buffer_29
  assign out_39 = decoder_2_out29 ? decoder_1_out0 : 32'bz;  // Controlled_Buffer controlled_buffer_30
  assign out_40 = decoder_2_out30 ? decoder_1_out0 : 32'bz;  // Controlled_Buffer controlled_buffer_31
  assign out_41 = decoder_2_out31 ? decoder_1_out0 : 32'bz;  // Controlled_Buffer controlled_buffer_32
  Pull_Resistor pull_resistor_1 (.node(out_39));
  Pull_Resistor pull_resistor_2 (.node(out_36));
  Pull_Resistor pull_resistor_3 (.node(out_35));
  Pull_Resistor pull_resistor_4 (.node(out_38));
  Pull_Resistor pull_resistor_5 (.node(out_37));
  Pull_Resistor pull_resistor_6 (.node(out_34));
  Pull_Resistor pull_resistor_7 (.node(out_41));
  Pull_Resistor pull_resistor_8 (.node(out_40));
  Pull_Resistor pull_resistor_9 (.node(out_31));
  Pull_Resistor pull_resistor_10 (.node(out_28));
  Pull_Resistor pull_resistor_11 (.node(out_26));
  Pull_Resistor pull_resistor_12 (.node(out_32));
  Pull_Resistor pull_resistor_13 (.node(out_30));
  Pull_Resistor pull_resistor_14 (.node(out_27));
  Pull_Resistor pull_resistor_15 (.node(out_29));
  Pull_Resistor pull_resistor_16 (.node(out_33));
  Pull_Resistor pull_resistor_17 (.node(out_19));
  Pull_Resistor pull_resistor_18 (.node(out_20));
  Pull_Resistor pull_resistor_19 (.node(out_18));
  Pull_Resistor pull_resistor_20 (.node(out_21));
  Pull_Resistor pull_resistor_21 (.node(out_25));
  Pull_Resistor pull_resistor_22 (.node(out_22));
  Pull_Resistor pull_resistor_23 (.node(out_24));
  Pull_Resistor pull_resistor_24 (.node(out_23));
  Pull_Resistor pull_resistor_25 (.node(out_12));
  Pull_Resistor pull_resistor_26 (.node(out_17));
  Pull_Resistor pull_resistor_27 (.node(out_15));
  Pull_Resistor pull_resistor_28 (.node(out_16));
  Pull_Resistor pull_resistor_29 (.node(out_14));
  Pull_Resistor pull_resistor_30 (.node(out_13));
  Pull_Resistor pull_resistor_31 (.node(out_11));
  Pull_Resistor pull_resistor_32 (.node(out_10));

  // Other names for the same wires on the sheet: player_y[4:0] = player_x
endmodule

module collision_check (
  input  [4:0] player_x,
  input  [4:0] player_x_1,
  input  [4:0] player_x_1_2,
  input  [4:0] ball_x,
  input  [4:0] ball_y,
  input  [4:0] coordinate_to_check,
  output hit_x,
  output hit_x_1,
  output hit_x_1_2,
  output hit_x_2,
  output hit_x_2_2
);

  wire comparator_1_eq, comparator_2_eq, comparator_3_eq, comparator_4_eq, comparator_5_lt, comparator_6_eq,
       comparator_7_eq, comparator_8_gt;
  wire [4:0] adder_1_out, subtractor_1_out;

  Adder #(.width(5)) adder_1 (.a(player_x), .b(5'b00010), .out(adder_1_out));  // open: cin, cout
  Subtractor #(.width(5)) subtractor_1 (.a(player_x), .b(5'b00010), .out(subtractor_1_out));  // open: bin, bout
  Comparator #(.width(5), .mode("unsigned")) comparator_1 (
    .a(player_x), .b(ball_x), .eq(comparator_1_eq));  // open: gt, lt
  Comparator #(.width(5), .mode("unsigned")) comparator_2 (
    .a(player_x_1), .b(ball_x), .eq(comparator_2_eq));  // open: gt, lt
  Comparator #(.width(5), .mode("unsigned")) comparator_3 (
    .a(player_x_1_2), .b(ball_x), .eq(comparator_3_eq));  // open: gt, lt
  Comparator #(.width(5)) comparator_4 (.a(ball_y), .b(coordinate_to_check), .eq(comparator_4_eq));  // open: gt, lt
  Comparator #(.width(5), .mode("unsigned")) comparator_5 (
    .a(player_x), .b(5'b11110), .lt(comparator_5_lt));  // open: gt, eq
  Comparator #(.width(5), .mode("unsigned")) comparator_6 (
    .a(adder_1_out), .b(ball_x), .eq(comparator_6_eq));  // open: gt, lt
  Comparator #(.width(5), .mode("unsigned")) comparator_7 (
    .a(subtractor_1_out), .b(ball_x), .eq(comparator_7_eq));  // open: gt, lt
  Comparator #(.width(5), .mode("unsigned")) comparator_8 (
    .a(player_x), .b(5'b00001), .gt(comparator_8_gt));  // open: eq, lt
  and and_1 (hit_x, comparator_1_eq, comparator_4_eq);
  and and_2 (hit_x_1, comparator_2_eq, comparator_4_eq);
  and and_3 (hit_x_1_2, comparator_3_eq, comparator_4_eq);
  and and_4 (hit_x_2, comparator_5_lt, comparator_6_eq, comparator_4_eq);
  and and_5 (hit_x_2_2, comparator_7_eq, comparator_4_eq);
endmodule

module dX (
  input  hit_ai_x,
  input  hit_ai_x_1,
  input  hit_ai_x_1_2,
  input  hit_ai_x_2,
  input  hit_ai_x_2_2,
  input  hit_player_x,
  input  hit_player_x_1,
  input  hit_player_x_1_2,
  input  hit_player_x_2,
  input  hit_player_x_2_2,
  input  btn_left,
  input  btn_right,
  input  freeze,
  input  [4:0] ball_x,
  input  game_clk,
  output dX
);

  wire and_1_out, and_2_out, comparator_1_eq, comparator_2_eq, d_ff_1_q, not_1_out, or_1_out, or_2_out,
       or_3_out, or_4_out, or_5_out, or_6_out, s_r_ff_1_q, s_r_ff_2_q;
  wire [2:0] priority_encoder_1_out;

  or or_1 (or_1_out, hit_ai_x, hit_player_x);
  or or_2 (or_2_out, hit_ai_x_1, hit_ai_x_2, hit_player_x_1, hit_player_x_2);
  or or_3 (or_3_out, hit_ai_x_1_2, hit_ai_x_2_2, hit_player_x_1_2, hit_player_x_2_2);
  or or_4 (or_4_out, or_2_out, or_3_out);
  and and_1 (and_1_out, btn_left, freeze);
  not not_1 (not_1_out, freeze);
  and and_2 (and_2_out, freeze, btn_right);
  S_R_Flip_Flop #(.trigger("falling")) s_r_ff_1 (
    .S(and_1_out), .clk(game_clk), .R(not_1_out), .Q(s_r_ff_1_q));  // open: Qn, preset, reset, en
  S_R_Flip_Flop #(.trigger("falling")) s_r_ff_2 (
    .S(and_2_out), .clk(game_clk), .R(not_1_out), .Q(s_r_ff_2_q));  // open: Qn, preset, reset, en
  Comparator #(.width(5), .mode("unsigned")) comparator_1 (
    .a(ball_x), .b({5{1'b0}}), .eq(comparator_1_eq));  // open: gt, lt
  or or_5 (or_5_out, comparator_1_eq, comparator_2_eq);
  Comparator #(.width(5), .mode("unsigned")) comparator_2 (
    .a(ball_x), .b({5{1'b1}}), .eq(comparator_2_eq));  // open: gt, lt
  or or_6 (or_6_out, or_1_out, or_4_out, s_r_ff_1_q, s_r_ff_2_q, or_5_out);
  D_Flip_Flop #(.trigger("falling")) d_ff_1 (.clk(or_6_out), .D(dX), .Q(d_ff_1_q));  // open: Qn, preset, en, reset
  Priority_Encoder priority_encoder_1 (
    .in0(1'b1), .in1(or_2_out), .in2(or_3_out), .in3(s_r_ff_1_q), .in4(s_r_ff_2_q), .in5(comparator_2_eq),
    .in6(comparator_1_eq), .out(priority_encoder_1_out));  // open: in7, en_in, gs, en_out
  Multiplexer #(.select(3), .enable("false")) multiplexer_1 (
    .in0(d_ff_1_q), .in1(1'b0), .in2(1'b1), .in3(1'b0), .in4(1'b1), .in5(1'b1), .in6(1'b0), .out(dX),
    .sel(priority_encoder_1_out));  // open: in7

  // Notes on the sheet:
  //   right_hit_any
  //   center_hit_any
  //   left_hit_any
  //   EVENT_HIT_RIGHT_WALL
  //   EVENT_HIT_LEFT_WALL
endmodule

module dY (
  input  hit_ai,
  input  hit_player,
  input  game_active,
  output hit_any,
  output dY
);

  wire d_ff_1_q, not_1_out;

  or or_1 (hit_any, hit_ai, hit_player);
  D_Flip_Flop #(.trigger("falling")) d_ff_1 (
    .clk(hit_any), .D(dY), .Q(d_ff_1_q), .en(game_active), .reset(not_1_out));  // open: Qn, preset
  not not_1 (not_1_out, game_active);
  Multiplexer #(.select(2), .enable("false")) multiplexer_1 (
    .in0(d_ff_1_q), .in1(1'b0), .in2(1'b1), .in3(1'b0), .out(dY), .sel({hit_player, hit_ai}));
endmodule

module Bresenham (
  input  hit_ai_x_1,
  input  hit_ai_x_1_2,
  input  hit_ai_x_2,
  input  hit_ai_x_2_2,
  input  hit_player_x_1,
  input  hit_player_x_1_2,
  input  hit_player_x_2,
  input  hit_player_x_2_2,
  input  hit_any,
  input  game_clk,
  input  game_active,
  output [4:0] slope_x,
  output [4:0] slope_y
);

  wire not_1_out;
  wire [1:0] Angle_Reg_q, or_1_out;

  or or_1 (or_1_out[0], hit_ai_x_1, hit_ai_x_1_2, hit_player_x_1, hit_player_x_1_2);
  or or_2 (or_1_out[1], hit_ai_x_2, hit_ai_x_2_2, hit_player_x_2, hit_player_x_2_2);
  Register #(.width(2)) Angle_Reg (.D(or_1_out), .en(hit_any), .Q(Angle_Reg_q), .clk(game_clk), .clr(not_1_out));
  not not_1 (not_1_out, game_active);
  Multiplexer #(.select(2), .width(5), .enable("false")) multiplexer_1 (
    .in0(5'b01000), .in1(5'b10000), .in2({5{1'b1}}), .out(slope_x), .sel(Angle_Reg_q));  // open: in3
  Multiplexer #(.select(2), .width(5), .enable("false")) multiplexer_2 (
    .in0({5{1'b1}}), .in1(5'b10000), .in2(5'b01000), .out(slope_y), .sel(Angle_Reg_q));  // open: in3

  // Notes on the sheet:
  //   border_hit
  //   corner_hit
endmodule

module freeze (
  input  game_clk,
  input  hit_x,
  input  hit_x_1,
  input  hit_x_1_2,
  input  btn_left,
  input  btn_right,
  output freeze
);

  wire and_1_out, and_2_out, d_ff_1_qn, or_1_out, or_2_out, shift_register_1_q0, shift_register_1_q1,
       shift_register_1_q2, shift_register_1_q3, shift_register_1_q4, shift_register_1_q5,
       shift_register_1_q6, shift_register_1_q7;

  or or_1 (or_1_out, hit_x, hit_x_1, hit_x_1_2);
  and and_1 (and_1_out, or_1_out, or_2_out);
  or or_2 (or_2_out, btn_left, btn_right);
  D_Flip_Flop #(.trigger("falling")) d_ff_1 (
    .clk(game_clk), .D(and_1_out), .Qn(d_ff_1_qn));  // open: Q, preset, en, reset
  and and_2 (and_2_out, d_ff_1_qn, and_1_out);
  Shift_Register #(.trigger("falling")) shift_register_1 (
    .shift(1'b1), .in(and_2_out), .clk(game_clk), .q0(shift_register_1_q0), .q1(shift_register_1_q1),
    .q2(shift_register_1_q2), .q3(shift_register_1_q3), .q4(shift_register_1_q4), .q5(shift_register_1_q5),
    .q6(shift_register_1_q6), .q7(shift_register_1_q7));  // open: out, load, clr, d0, d1, d2, d3, d4, d5, d6, d7
  or or_3 (freeze, shift_register_1_q7, shift_register_1_q6, shift_register_1_q5, shift_register_1_q4, shift_register_1_q3, shift_register_1_q2, shift_register_1_q1, shift_register_1_q0);
endmodule

module game_active (
  input  [4:0] ball_y,
  input  btn_left,
  input  btn_right,
  input  btn_reset,
  input  interrupt_start,
  input  name_is_valid,
  input  game_clk,
  output [3:0] player_fails,
  output [3:0] ai_fails,
  output player_loser,
  output game_active
);

  wire and_1_out, comparator_1_eq, comparator_2_eq, comparator_3_eq, comparator_4_eq, not_1_out, not_2_out,
       or_1_out, or_2_out, or_3_out, or_4_out, or_5_out, xnor_1_out, xnor_2_out;

  Comparator #(.width(5), .mode("unsigned")) comparator_1 (
    .a(ball_y), .b({5{1'b0}}), .eq(comparator_1_eq));  // open: gt, lt
  Comparator #(.width(5), .mode("unsigned")) comparator_2 (
    .a(ball_y), .b({5{1'b1}}), .eq(comparator_2_eq));  // open: gt, lt
  or or_1 (or_1_out, comparator_1_eq, comparator_2_eq);
  not not_1 (not_1_out, btn_left);
  not not_2 (not_2_out, btn_right);
  or or_2 (or_2_out, or_1_out, btn_reset);
  xnor xnor_1 (xnor_1_out, btn_left, not_1_out);
  or or_3 (or_3_out, xnor_1_out, xnor_2_out);
  xnor xnor_2 (xnor_2_out, btn_right, not_2_out);
  and and_1 (and_1_out, name_is_valid, or_3_out);
  S_R_Flip_Flop #(.trigger("high")) s_r_ff_1 (
    .S(and_1_out), .clk(game_clk), .R(or_2_out), .Q(game_active));  // open: Qn, preset, reset, en
  Counter #(.width(4), .max('hf)) counter_1 (
    .Q(player_fails), .clk(comparator_1_eq), .clr(or_5_out));  // open: load, D, count, carry
  Counter #(.width(4), .max('hf)) counter_2 (
    .Q(ai_fails), .clk(comparator_2_eq), .clr(or_5_out));  // open: load, D, count, carry
  Comparator #(.width(4), .mode("unsigned")) comparator_3 (
    .a(player_fails), .b(4'b0101), .eq(comparator_3_eq));  // open: gt, lt
  or or_4 (or_4_out, comparator_3_eq, comparator_4_eq);
  Comparator #(.width(4), .mode("unsigned")) comparator_4 (
    .a(4'b0101), .b(ai_fails), .eq(comparator_4_eq));  // open: gt, lt
  or or_5 (or_5_out, btn_reset, or_4_out);
  D_Flip_Flop d_ff_1 (.clk(or_4_out), .D(or_4_out), .Q(player_loser), .reset(interrupt_start));  // open: Qn, preset, en

  // Other names for the same wires on the sheet: L = btn_left; R = btn_right; Reset = btn_reset

  // Notes on the sheet:
  //   EVENT_HIT_TOP_WALL
  //   EVENT_HIT_BOTTOM_WALL
endmodule

module player_score_game_speed (
  input  hit_player,
  input  f1_wrtie,
  input  btn_reset,
  input  game_clk,
  output [7:0] game_speed,
  output [7:0] player_score
);

  wire and_1_out, counter_2_carry, d_ff_1_qn, not_1_out, or_1_out, s_r_ff_1_q;
  wire [2:0] counter_3_q;

  not not_1 (not_1_out, hit_player);
  S_R_Flip_Flop #(.trigger("falling")) s_r_ff_1 (
    .S(hit_player), .clk(game_clk), .R(not_1_out), .Q(s_r_ff_1_q));  // open: Qn, preset, reset, en
  Counter counter_1 (.Q(player_score), .clk(s_r_ff_1_q), .clr(or_1_out));  // open: load, D, count, carry
  Counter #(.width(4), .max('h5)) counter_2 (
    .carry(counter_2_carry), .clk(s_r_ff_1_q), .clr(or_1_out));  // open: load, D, count, Q
  or or_1 (or_1_out, f1_wrtie, btn_reset);
  D_Flip_Flop #(.trigger("falling")) d_ff_1 (
    .clk(game_clk), .D(counter_2_carry), .Qn(d_ff_1_qn));  // open: Q, preset, en, reset
  and and_1 (and_1_out, d_ff_1_qn, counter_2_carry);
  Counter #(.width(3), .max('h7), .ongoal("stay")) counter_3 (
    .count(and_1_out), .Q(counter_3_q), .clk(game_clk), .clr(or_1_out));  // open: load, D, carry
  Multiplexer #(.select(3), .width(8), .enable("false")) multiplexer_1 (
    .in0(8'h40), .in1(8'h38), .in2(8'h35), .in3(8'h30), .in4(8'h28), .in5(8'h25), .in6(8'h20), .in7(8'h15),
    .out(game_speed), .sel(counter_3_q));
endmodule

module PROCESSOR_LOGIC (
  input  cdm8_clk,
  input  player_loser,
  input  [7:0] player_score,
  input  btn_input_name,
  input  btn_reset,
  input  game_active,
  input  [6:0] kbd_data,
  input  kbd_is_ready,
  output f1_write,
  output [6:0] I_O_data_read,
  output interrupt_start,
  output clear_name_screen,
  output name_is_valid,
  output clear_kbd,
  output name_screen_enable,
  output kbd_enable
);

  wire and_3_out, and_4_out, and_5_out, and_6_out, and_7_out, and_8_out, and_9_out, and_10_out, and_12_out,
       and_13_out, and_14_out, arbiter_1_p4, buff_sel, cdm_8_mark5_1_p4, cdm_8_mark5_1_p5, cdm_8_mark5_1_p7,
       cdm_8_mark5_1_p8, cdm_8_mark5_1_p9, cdm_8_mark5_1_p10, cdm_8_mark5_1_p11, cdm_8_mark5_1_p12, code,
       comparator_1_eq, comparator_2_eq, comparator_3_eq, comparator_4_eq, comparator_5_eq, data, I_O_sel,
       IAck, init_table, input_enable, IRQ, mem, multiplexer_3_out, not_1_out, not_2_out, not_3_out,
       or_1_out, RAM, rd_wr, set_name;
  wire [0:0] d_ff_1_q;
  wire [1:0] priority_encoder_1_out;
  wire [2:0] vec;
  wire [3:0] I_O_addr;
  wire [7:0] bit_extender_2_out, buff_addr, buff_data, cdm_8_mark5_1_p16, cdm_8_mark5_1_p17, I_O_data_read_t,
       init_addr, init_data, multiplexer_1_out, multiplexer_2_out;
  wire [7:4] cdm_8_mark5_1_p15;

  // Probe on cdm_8_mark5_1_p8
  // Probe on cdm_8_mark5_1_p7
  // Probe on cdm_8_mark5_1_p5
  // Probe on cdm_8_mark5_1_p4
  // Probe on cdm_8_mark5_1_p11
  // Probe on cdm_8_mark5_1_p10
  // Probe on cdm_8_mark5_1_p9
  // CdM_8_mark5 cdm_8_mark5_1: pin names not known; wires that end beside it: IRQ, vec, IAck, cdm_8_mark5_1_p4, cdm_8_mark5_1_p5, cdm8_clk, cdm_8_mark5_1_p7, cdm_8_mark5_1_p8, cdm_8_mark5_1_p9, cdm_8_mark5_1_p10, cdm_8_mark5_1_p11, cdm_8_mark5_1_p12, mem, rd_wr, {cdm_8_mark5_1_p15, I_O_addr}, cdm_8_mark5_1_p16, cdm_8_mark5_1_p17
  assign cdm_8_mark5_1_p17 = rd_wr ? I_O_data_read_t : 8'bz;  // Controlled_Buffer controlled_buffer_1
  Pull_Resistor pull_resistor_1 (.node(code));
  Decoder decoder_1 (.out0(code), .out1(data), .sel(cdm_8_mark5_1_p12), .en(mem));
  Pull_Resistor pull_resistor_2 (.node(data));
  assign I_O_data_read_t = not_1_out ? cdm_8_mark5_1_p16 : 8'bz;  // Controlled_Buffer controlled_buffer_2
  not not_1 (not_1_out, rd_wr);
  Multiplexer #(.select(2), .width(8), .enable("false")) multiplexer_1 (
    .in0({cdm_8_mark5_1_p15, I_O_addr}), .in1(init_addr), .in2(buff_addr), .out(multiplexer_1_out),
    .sel(priority_encoder_1_out));  // open: in3
  Priority_Encoder #(.select(2)) priority_encoder_1 (
    .in0(1'b1), .in1(init_table), .in2(set_name), .out(priority_encoder_1_out));  // open: in3, gs, en_out, en_in
  Multiplexer #(.select(2), .width(8), .enable("false")) multiplexer_2 (
    .in0(I_O_data_read_t), .in1(init_data), .in2(buff_data), .out(multiplexer_2_out),
    .sel(priority_encoder_1_out));  // open: in3
  not not_2 (not_2_out, rd_wr);
  or or_1 (or_1_out, not_2_out, init_table);
  Multiplexer #(.select(2), .enable("false")) multiplexer_3 (
    .in0(RAM), .in1(init_table), .in2(buff_sel), .out(multiplexer_3_out), .sel(priority_encoder_1_out));  // open: in3
  and and_1 (I_O_sel, cdm_8_mark5_1_p15[4], cdm_8_mark5_1_p15[5], cdm_8_mark5_1_p15[6], cdm_8_mark5_1_p15[7], data);
  and and_2 (RAM, ~I_O_sel, data);  // AND_Gate
  ROM rom_1 (.addr({cdm_8_mark5_1_p15, I_O_addr}), .data(I_O_data_read_t), .sel(code));
  RAM #(.bus("separate")) ram_1 (
    .addr(multiplexer_1_out), .din(multiplexer_2_out), .data(I_O_data_read_t), .str(or_1_out),
    .sel(multiplexer_3_out), .clk(cdm8_clk), .ld(not_3_out));  // open: clr
  not not_3 (not_3_out, or_1_out);
  name_is_valid name_is_valid_1 (
    .RAM_data(multiplexer_2_out), .RAM_addr(multiplexer_1_out), .rd_wr(or_1_out),
    .input_enable(input_enable), .cdm8_clk(cdm8_clk), .name_is_valid(name_is_valid));
  Comparator #(.width(4), .mode("unsigned")) comparator_1 (
    .a(I_O_addr), .b(4'b0010), .eq(comparator_1_eq));  // open: gt, lt
  Comparator #(.width(4), .mode("unsigned")) comparator_2 (
    .a(I_O_addr), .b(4'b0011), .eq(comparator_2_eq));  // open: gt, lt
  Comparator #(.width(4), .mode("unsigned")) comparator_3 (
    .a(I_O_addr), .b(4'b0001), .eq(comparator_3_eq));  // open: gt, lt
  and and_3 (and_3_out, comparator_3_eq, I_O_sel);
  and and_4 (and_4_out, comparator_1_eq, I_O_sel);
  and and_5 (and_5_out, comparator_2_eq, I_O_sel);
  Comparator #(.width(4), .mode("unsigned")) comparator_4 (
    .a(I_O_addr), .b(4'b0100), .eq(comparator_4_eq));  // open: gt, lt
  and and_6 (and_6_out, comparator_4_eq, I_O_sel);
  init_records_table u_INIT_TABLE (
    .cdm8_clk(cdm8_clk), .init_table(init_table), .init_data(init_data), .init_addr(init_addr));
  Comparator #(.width(4), .mode("unsigned")) comparator_5 (
    .a(I_O_addr), .b(4'b0101), .eq(comparator_5_eq));  // open: gt, lt
  and and_7 (and_7_out, comparator_5_eq, I_O_sel);
  LED led_1 (.in(and_3_out));
  Bit_Extender #(.out_width(7)) bit_extender_1 (.in(I_O_data_read_t), .out(I_O_data_read));
  and and_8 (and_8_out, ~rd_wr, and_4_out);  // AND_Gate
  and and_9 (and_9_out, rd_wr, and_5_out);
  and and_10 (and_10_out, ~rd_wr, and_6_out);  // AND_Gate
  assign bit_extender_2_out = {{7{1'b0}}, init_table};  // Bit_Extender bit_extender_2
  and and_11 (f1_write, ~rd_wr, and_3_out);  // AND_Gate
  D_Flip_Flop #(.trigger("falling")) d_ff_1 (
    .clk(cdm8_clk), .D(I_O_data_read_t[0]), .Q(d_ff_1_q[0]), .en(and_8_out));  // open: Qn, preset, reset
  assign I_O_data_read_t = and_9_out ? player_score : 8'bz;  // Controlled_Buffer controlled_buffer_3
  assign I_O_data_read_t = and_12_out ? bit_extender_2_out : 8'bz;  // Controlled_Buffer controlled_buffer_4
  and and_12 (and_12_out, rd_wr, and_7_out);
  assign I_O_data_read_t = and_13_out ? {player_loser, {6{1'b0}}, d_ff_1_q[0]} : 8'bz;  // Controlled_Buffer controlled_buffer_5
  and and_13 (and_13_out, rd_wr, and_4_out);
  D_Flip_Flop #(.trigger("falling")) u_input_enable (
    .clk(cdm8_clk), .D(I_O_data_read_t[0]), .Q(input_enable), .en(and_10_out));  // open: Qn, preset, reset
  and and_14 (and_14_out, d_ff_1_q[0], player_loser);
  kbd_controller KBD_CONTROLLER (
    .input_enable(input_enable), .btn_input_name(btn_input_name), .btn_reset(btn_reset), .cdm8_clk(cdm8_clk),
    .game_active(game_active), .player_loser(player_loser), .kbd_data(kbd_data), .kbd_is_ready(kbd_is_ready),
    .clear_name_screen(clear_name_screen), .buff_sel(buff_sel), .buff_addr(buff_addr), .clear_kbd(clear_kbd),
    .buff_data(buff_data), .name_screen_enable(name_screen_enable), .kbd_enable(kbd_enable),
    .set_name(set_name));
  assign vec = arbiter_1_p4 ? 3'b100 : 3'bz;  // Controlled_Buffer controlled_buffer_6
  // arbiter arbiter_1: pin names not known; wires that end beside it: IRQ, IAck, cdm8_clk, arbiter_1_p4, and_14_out, and_9_out, 1'b0, 1'b0
  and and_15 (interrupt_start, IAck, arbiter_1_p4);

  // Other names for the same wires on the sheet: I_O_data_write[7:0] = I_O_data_read_t

  // Notes on the sheet:
  //   instr_mem
  //   contents of rom_1 (hex, n*v repeats v):
  //   d0 f5 b1 5 e0 8 ee 2 cd f0 d0 3d d1 10 d2 5 a e0 1e a1 d3 0 a7 8c d3 9 1d 8a ee 10 d6 83 d1 1 d0 f2
  //   a1 d0 f4 a1 c1 d1 30 c1 d1 80 c1 d9 c5 d5 ee 31 ce d0 0 d1 f4 a4 d0 f3 b1 d0 3d d2 42 72 e0 52 b2 bb
  //   77 ec 4c 8c ee 50 d6 5b ee 52 ee 3f d6 83 d0 1 d1 f4 a4 cf d9 d2 41 bb ad c0 c1 c2 c3 d 8d d0 0 d2 8
  //   a e0 73 b3 a7 8c 8d 8a ee 69 c7 c6 c5 c4 78 e0 81 9 89 b5 a9 8a ee 77 a3 d7 d0 3d d3 5 f e0 b0 b2 c2
  //   ba c0 c3 d6 b4 c7 c4 d1 f1 d2 20 a6 c6 8e c0 c3 d3 8 f e0 a7 b8 a4 8e 8b ee 9e c7 c4 d2 a a6 8c 8b
  //   ee 87 d2 a a6 d7 d1 f1 d0 0 d3 64 7b eb c2 3b e 8c ee b8 d3 30 13 a7 d0 0 d3 a 7b eb d2 3b e 8c ee
  //   c8 d3 30 13 a7 d3 30 1b a7 d7 29*0 34
  //   data_mem
  //   RECORDS_SCREEN
  //   RECORDS_INTERRUPT
  //   NAME_INPUT
  //   RECORDS_TABLE_INIT
  //   0xf2  -> status register 
  //   0xf3  -> data register 
  //   vec == 4
  //   ldi r0, 0xf0
  //   ldi r1, 1
  //   st r0, r1
  //   status = 10000000b  если символ готов 
  //   status = 00000001b  если прерывания разрешены 
  //   status = 10000001b  если и символ готов, и прерывания разрешены
  //   Чтобы разрешить прерывания от клавиатуры, программа должна записать 1 в бит 0 регистра 0xf0
endmodule

module init_records_table (
  input  cdm8_clk,
  output init_table,
  output [7:0] init_data,
  output [7:0] init_addr
);

  wire counter_1_carry, not_1_out;
  wire [5:0] counter_1_q;
  wire [7:0] bit_extender_1_out;

  not not_1 (not_1_out, counter_1_carry);
  D_Flip_Flop d_ff_1 (
    .clk(cdm8_clk), .D(1'b1), .Q(init_table), .en(not_1_out), .reset(counter_1_carry));  // open: Qn, preset
  Counter #(.width(6), .max('h2c), .ongoal("stay")) counter_1 (
    .count(init_table), .Q(counter_1_q), .carry(counter_1_carry), .clk(cdm8_clk));  // open: load, D, clr
  assign bit_extender_1_out = {{2{1'b0}}, counter_1_q};  // Bit_Extender bit_extender_1
  ROM rom_1 (.addr(bit_extender_1_out), .data(init_data), .sel(1'b1));
  Adder adder_1 (.a(bit_extender_1_out), .b(8'h10), .out(init_addr));  // open: cin, cout

  // Notes on the sheet:
  //   contents of rom_1 (hex, n*v repeats v):
  //   0 49 72 74 65 67 6f 76 0 0 4e 61 7a 61 72 6f 76 0 0 42 6f 6e 64 61 72 65 76 0 49 76 61 6e 6f 76 0 0
  //   0 50 65 74 72 6f 76
endmodule

module symbol_is_valid (
  input  [6:0] kbd_symbol,
  output is_valid
);

  wire and_1_out, and_2_out, comparator_1_eq, comparator_2_eq, comparator_3_eq, comparator_4_gt,
       comparator_5_lt, comparator_6_gt, comparator_7_lt;

  Comparator #(.width(7), .mode("unsigned")) comparator_1 (
    .a(kbd_symbol), .b(7'b0100000), .eq(comparator_1_eq));  // open: gt, lt
  Comparator #(.width(7), .mode("unsigned")) comparator_2 (
    .a(kbd_symbol), .b(7'b1011111), .eq(comparator_2_eq));  // open: gt, lt
  Comparator #(.width(7), .mode("unsigned")) comparator_3 (
    .a(kbd_symbol), .b(7'b0001000), .eq(comparator_3_eq));  // open: gt, lt
  Comparator #(.width(7), .mode("unsigned")) comparator_4 (
    .a(kbd_symbol), .b(7'b1000000), .gt(comparator_4_gt));  // open: eq, lt
  Comparator #(.width(7), .mode("unsigned")) comparator_5 (
    .a(kbd_symbol), .b(7'b1011011), .lt(comparator_5_lt));  // open: gt, eq
  Comparator #(.width(7), .mode("unsigned")) comparator_6 (
    .a(kbd_symbol), .b(7'b1100000), .gt(comparator_6_gt));  // open: eq, lt
  Comparator #(.width(7), .mode("unsigned")) comparator_7 (
    .a(kbd_symbol), .b(7'b1111011), .lt(comparator_7_lt));  // open: gt, eq
  and and_1 (and_1_out, comparator_4_gt, comparator_5_lt);
  and and_2 (and_2_out, comparator_6_gt, comparator_7_lt);
  or or_1 (is_valid, comparator_1_eq, comparator_2_eq, comparator_3_eq, and_1_out, and_2_out);

  // Notes on the sheet:
  //   Пробел
  //   Нижнее подчеркивание
  //   Стереть
  //   A-Z
  //   a-z
endmodule

module name_is_valid (
  input  [7:0] RAM_data,
  input  [7:0] RAM_addr,
  input  rd_wr,
  input  input_enable,
  input  cdm8_clk,
  output name_is_valid
);

  wire and_1_out, comparator_1_eq, comparator_2_eq, comparator_3_eq, comparator_4_eq;
  wire [7:0] register_1_q;

  Comparator #(.mode("unsigned")) comparator_1 (.a(RAM_addr), .b({8{1'b0}}), .eq(comparator_1_eq));  // open: gt, lt
  and and_1 (and_1_out, comparator_1_eq, rd_wr, input_enable);
  Register register_1 (.D(RAM_data), .en(and_1_out), .Q(register_1_q), .clk(cdm8_clk));  // open: clr
  Comparator #(.mode("unsigned")) comparator_2 (.a(register_1_q), .b({8{1'b0}}), .eq(comparator_2_eq));  // open: gt, lt
  Comparator #(.mode("unsigned")) comparator_3 (.a(register_1_q), .b(8'h20), .eq(comparator_3_eq));  // open: gt, lt
  Comparator #(.mode("unsigned")) comparator_4 (.a(register_1_q), .b(8'h5f), .eq(comparator_4_eq));  // open: gt, lt
  nor nor_1 (name_is_valid, comparator_2_eq, comparator_3_eq, comparator_4_eq);
endmodule

module kbd_controller (
  input  input_enable,
  input  btn_input_name,
  input  btn_reset,
  input  cdm8_clk,
  input  game_active,
  input  player_loser,
  input  [6:0] kbd_data,
  input  kbd_is_ready,
  output clear_name_screen,
  output buff_sel,
  output [7:0] buff_addr,
  output set_name,
  output clear_kbd,
  output [7:0] buff_data,
  output name_screen_enable,
  output kbd_enable
);

  wire and_2_out, comparator_1_eq, comparator_2_eq, counter_2_carry, kbd_sel, NAME_BUFFER_CLEANING_q,
       or_1_out, s_r_ff_1_q, symbol_is_valid;
  wire [3:0] counter_1_q, counter_2_q;
  wire [7:0] bit_extender_1_out, bit_extender_3_out, kbd_addr, kbd_data_t;

  and and_1 (kbd_sel, kbd_is_ready, symbol_is_valid);
  assign bit_extender_1_out = {{1{1'b0}}, kbd_data};  // Bit_Extender bit_extender_1
  symbol_is_valid symbol_is_valid_1 (.kbd_symbol(kbd_data), .is_valid(symbol_is_valid));
  Multiplexer #(.width(8), .enable("false")) multiplexer_1 (
    .in0(bit_extender_1_out), .in1({8{1'b0}}), .out(kbd_data_t), .sel(comparator_1_eq));
  Comparator #(.mode("unsigned")) comparator_1 (
    .a(bit_extender_1_out), .b(8'h8), .eq(comparator_1_eq));  // open: gt, lt
  Counter #(.width(4), .max('h8), .ongoal("stay"), .trigger("falling")) counter_1 (
    .load(comparator_1_eq), .Q(counter_1_q), .clk(kbd_sel), .clr(clear_kbd));  // open: D, count, carry
  and and_2 (and_2_out, input_enable, btn_input_name);
  Comparator #(.width(4), .mode("unsigned")) comparator_2 (
    .a(counter_1_q), .b(4'b1000), .eq(comparator_2_eq));  // open: gt, lt
  assign kbd_addr = {{4{1'b0}}, counter_1_q};  // Bit_Extender bit_extender_2
  S_R_Flip_Flop s_r_ff_1 (
    .S(and_2_out), .clk(cdm8_clk), .R(game_active), .Q(s_r_ff_1_q), .Qn(clear_kbd), .reset(or_1_out));  // open: preset, en
  or or_1 (or_1_out, game_active, player_loser, btn_reset, comparator_2_eq);
  or or_2 (clear_name_screen, btn_reset, and_2_out);
  not not_1 (kbd_enable, clear_kbd);
  or or_3 (set_name, btn_reset, s_r_ff_1_q);
  and and_3 (name_screen_enable, kbd_enable, symbol_is_valid);
  Counter #(.width(4), .max('h8), .ongoal("stay")) counter_2 (
    .count(clear_name_screen), .Q(counter_2_q), .carry(counter_2_carry), .clk(cdm8_clk), .clr(clear_kbd));  // open: load, D
  D_Flip_Flop NAME_BUFFER_CLEANING (
    .clk(clear_name_screen), .D(clear_name_screen), .Q(NAME_BUFFER_CLEANING_q), .reset(counter_2_carry));  // open: Qn, preset, en
  assign bit_extender_3_out = {{4{1'b0}}, counter_2_q};  // Bit_Extender bit_extender_3
  Multiplexer #(.enable("false")) multiplexer_2 (
    .in0(kbd_sel), .in1(NAME_BUFFER_CLEANING_q), .out(buff_sel), .sel(NAME_BUFFER_CLEANING_q));
  Multiplexer #(.width(8), .enable("false")) multiplexer_3 (
    .in0(kbd_addr), .in1(bit_extender_3_out), .out(buff_addr), .sel(NAME_BUFFER_CLEANING_q));
  Multiplexer #(.width(8), .enable("false")) multiplexer_4 (
    .in0(kbd_data_t), .in1({8{1'b0}}), .out(buff_data), .sel(NAME_BUFFER_CLEANING_q));

  // Notes on the sheet:
  //   SET_NAME
endmodule

module bcd (
  input  [7:0] bus_0,
  input  hit_player,
  input  f1_wrtie,
  input  btn_reset,
  input  game_clk,
  output [3:0] bus_0_2,
  output [3:0] bus_0_3,
  output [3:0] bus_0_4,
  output [3:0] bus_0_5,
  output [7:0] bus_0_6,
  output [7:0] game_speed,
  output [3:0] player_score_one,
  output [3:0] player_score_ten
);

  wire adder_2_cout, and_1_out, and_2_out, counter_1_carry, counter_2_carry, d_ff_1_qn, not_1_out, or_1_out,
       or_2_out, s_r_ff_1_q;
  wire [2:0] counter_4_q;
  wire [3:0] multiplexer_1_out;

  // Probe on bus_0[7:4]
  // Probe on bus_0[3:0]
  // Probe on bus_0
  S_R_Flip_Flop #(.trigger("falling")) s_r_ff_1 (
    .S(hit_player), .clk(game_clk), .R(not_1_out), .Q(s_r_ff_1_q));  // open: Qn, preset, reset, en
  not not_1 (not_1_out, hit_player);
  or or_1 (or_1_out, bus_0[1], bus_0[2]);
  Counter #(.width(4), .max('h9)) counter_1 (
    .Q(player_score_one), .carry(counter_1_carry), .clk(s_r_ff_1_q), .clr(or_2_out));  // open: load, D, count
  and and_1 (and_1_out, or_1_out, bus_0[3]);
  Counter #(.width(4), .max('h5)) counter_2 (
    .carry(counter_2_carry), .clk(s_r_ff_1_q), .clr(or_2_out));  // open: load, D, count, Q
  or or_2 (or_2_out, f1_wrtie, btn_reset);
  Counter #(.width(4), .max('h7), .trigger("falling")) counter_3 (
    .Q(player_score_ten), .clk(counter_1_carry), .clr(or_2_out));  // open: load, D, count, carry
  Multiplexer #(.width(4)) multiplexer_1 (
    .in0(4'b0000), .in1(4'b0110), .out(multiplexer_1_out), .sel(and_1_out));  // open: en
  D_Flip_Flop #(.trigger("falling")) d_ff_1 (
    .clk(game_clk), .D(counter_2_carry), .Qn(d_ff_1_qn));  // open: Q, preset, en, reset
  and and_2 (and_2_out, d_ff_1_qn, counter_2_carry);
  Adder #(.width(4)) adder_1 (.a(bus_0[7:4]), .b(4'b0000), .out(bus_0_4), .cin(adder_2_cout));  // open: cout
  Adder #(.width(4)) adder_2 (.a(bus_0[3:0]), .b(multiplexer_1_out), .out(bus_0_5), .cout(adder_2_cout));  // open: cin
  Counter #(.width(3), .max('h7), .ongoal("stay")) counter_4 (
    .count(and_2_out), .Q(counter_4_q), .clk(game_clk), .clr(or_2_out));  // open: load, D, carry
  // Probe on {bus_0_4, bus_0_5}
  Multiplexer #(.select(3), .width(8), .enable("false")) multiplexer_2 (
    .in0(8'h40), .in1(8'h38), .in2(8'h35), .in3(8'h30), .in4(8'h28), .in5(8'h25), .in6(8'h20), .in7(8'h15),
    .out(game_speed), .sel(counter_4_q));

  assign bus_0_2 = bus_0[7:4];
  assign bus_0_3 = bus_0[3:0];
  assign bus_0_6 = {bus_0_4, bus_0_5};
endmodule
